// Logisim project Logic Components.circ as structural Verilog: 23 circuits, main circuit full adder
module full_adder (
  input  A,
  input  B,
  input  Cin,
  output S,
  output Cout
);

  wire and_1_out, and_2_out, xor_1_out;

  xor xor_1 (xor_1_out, A, B);
  and and_1 (and_1_out, Cin, xor_1_out);
  and and_2 (and_2_out, A, B);
  xor xor_2 (S, xor_1_out, Cin);
  or or_1 (Cout, and_1_out, and_2_out);
endmodule

module _1x2_MUX (
  input  A0,
  input  A1,
  input  sel,
  output Q0
);

  wire and_1_out, and_2_out, not_1_out;

  not not_1 (not_1_out, sel);
  and and_1 (and_1_out, A0, not_1_out);
  and and_2 (and_2_out, A1, sel);
  or or_1 (Q0, and_1_out, and_2_out);
endmodule

module _2x4_MUX (
  input  cntl1,
  input  cntl0,
  input  A0,
  input  A1,
  input  A2,
  input  A3,
  output Q0
);

  wire and_1_out, and_2_out, and_3_out, and_4_out, and_5_out, and_6_out, and_7_out, and_8_out, not_1_out,
       not_2_out, not_3_out, not_4_out;

  not not_1 (not_1_out, cntl0);
  and and_1 (and_1_out, not_1_out, not_2_out);
  not not_2 (not_2_out, cntl1);
  and and_2 (and_2_out, cntl0, not_3_out);
  not not_3 (not_3_out, cntl1);
  not not_4 (not_4_out, cntl0);
  and and_3 (and_3_out, not_4_out, cntl1);
  and and_4 (and_4_out, cntl0, cntl1);
  and and_5 (and_5_out, A0, and_1_out);
  and and_6 (and_6_out, A1, and_2_out);
  and and_7 (and_7_out, A2, and_3_out);
  and and_8 (and_8_out, A3, and_4_out);
  or or_1 (Q0, and_5_out, and_6_out, and_7_out, and_8_out);
endmodule

module _8_bit_register (
  input  A0,
  input  A1,
  input  A2,
  input  A3,
  input  A4,
  input  A5,
  input  A6,
  input  A7,
  input  write,
  input  read,
  output Q0,
  output Q1,
  output Q2,
  output Q3,
  output Q4,
  output Q5,
  output Q6,
  output Q7
);

  wire d_latch_1_q, d_latch_2_q, d_latch_3_q, d_latch_4_q, d_latch_5_q, d_latch_6_q, d_latch_7_q, d_latch_8_q;

  D_latch d_latch_1 (.D(A0), .enable(write), .Q(d_latch_1_q));  // open: Q_prime
  D_latch d_latch_2 (.D(A1), .enable(write), .Q(d_latch_2_q));  // open: Q_prime
  D_latch d_latch_3 (.D(A2), .enable(write), .Q(d_latch_3_q));  // open: Q_prime
  D_latch d_latch_4 (.D(A3), .enable(write), .Q(d_latch_4_q));  // open: Q_prime
  D_latch d_latch_5 (.D(A4), .enable(write), .Q(d_latch_5_q));  // open: Q_prime
  D_latch d_latch_6 (.D(A5), .enable(write), .Q(d_latch_6_q));  // open: Q_prime
  D_latch d_latch_7 (.D(A6), .enable(write), .Q(d_latch_7_q));  // open: Q_prime
  D_latch d_latch_8 (.D(A7), .enable(write), .Q(d_latch_8_q));  // open: Q_prime
  and and_1 (Q0, d_latch_1_q, read);
  and and_2 (Q1, d_latch_2_q, read);
  and and_3 (Q2, d_latch_3_q, read);
  and and_4 (Q3, d_latch_4_q, read);
  and and_5 (Q4, d_latch_5_q, read);
  and and_6 (Q5, d_latch_6_q, read);
  and and_7 (Q6, d_latch_7_q, read);
  and and_8 (Q7, d_latch_8_q, read);
endmodule

module D_latch (
  input  D,
  input  enable,
  output Q,
  output Q_prime
);

  wire nand_1_out, nand_2_out;

  nand nand_1 (nand_1_out, D, enable);
  nand nand_2 (nand_2_out, enable, nand_1_out);
  nand nand_3 (Q, nand_1_out, Q_prime);
  nand nand_4 (Q_prime, Q, nand_2_out);
endmodule

module _8_32_splitter (
  input  A7,
  input  A6,
  input  A5,
  input  A4,
  input  A3,
  input  A2,
  input  A1,
  input  A0,
  output Q37,
  output Q36,
  output Q35,
  output Q34,
  output Q33,
  output Q32,
  output Q31,
  output Q30,
  output Q27,
  output Q26,
  output Q25,
  output Q24,
  output Q23,
  output Q22,
  output Q21,
  output Q20,
  output Q17,
  output Q16,
  output Q15,
  output Q14,
  output Q13,
  output Q12,
  output Q11,
  output Q10,
  output Q07,
  output Q06,
  output Q05,
  output Q04,
  output Q03,
  output Q02,
  output Q01,
  output Q00
);

  buf buffer_1 (Q37, A7);
  buf buffer_2 (Q36, A6);
  buf buffer_3 (Q33, A3);
  buf buffer_4 (Q35, A5);
  buf buffer_5 (Q34, A4);
  buf buffer_6 (Q32, A2);
  buf buffer_7 (Q27, A7);
  buf buffer_8 (Q31, A1);
  buf buffer_9 (Q30, A0);
  buf buffer_10 (Q26, A6);
  buf buffer_11 (Q24, A4);
  buf buffer_12 (Q23, A3);
  buf buffer_13 (Q25, A5);
  buf buffer_14 (Q22, A2);
  buf buffer_15 (Q20, A0);
  buf buffer_16 (Q17, A7);
  buf buffer_17 (Q21, A1);
  buf buffer_18 (Q13, A3);
  buf buffer_19 (Q14, A4);
  buf buffer_20 (Q16, A6);
  buf buffer_21 (Q15, A5);
  buf buffer_22 (Q10, A0);
  buf buffer_23 (Q12, A2);
  buf buffer_24 (Q07, A7);
  buf buffer_25 (Q11, A1);
  buf buffer_26 (Q04, A4);
  buf buffer_27 (Q03, A3);
  buf buffer_28 (Q06, A6);
  buf buffer_29 (Q05, A5);
  buf buffer_30 (Q00, A0);
  buf buffer_31 (Q01, A1);
  buf buffer_32 (Q02, A2);
endmodule

module _1_of_4 (
  input  A1,
  input  A0,
  output Q3,
  output Q2,
  output Q1,
  output Q0
);

  wire not_1_out, not_2_out, not_3_out, not_4_out;

  and and_1 (Q2, A1, not_1_out);
  and and_2 (Q3, A1, A0);
  not not_1 (not_1_out, A0);
  not not_2 (not_2_out, A1);
  not not_3 (not_3_out, A1);
  and and_3 (Q0, not_2_out, not_4_out);
  and and_4 (Q1, not_3_out, A0);
  not not_4 (not_4_out, A0);
endmodule

module _8_4_input_OR_gates (
  input  D7,
  input  D6,
  input  D5,
  input  D4,
  input  D3,
  input  D2,
  input  D1,
  input  D0,
  input  C7,
  input  C6,
  input  C5,
  input  C4,
  input  C3,
  input  C2,
  input  C1,
  input  C0,
  input  B7,
  input  B6,
  input  B5,
  input  B4,
  input  B3,
  input  B2,
  input  B1,
  input  B0,
  input  A7,
  input  A6,
  input  A5,
  input  A4,
  input  A3,
  input  A2,
  input  A1,
  input  A0,
  output Q7,
  output Q6,
  output Q5,
  output Q4,
  output Q3,
  output Q2,
  output Q1,
  output Q0
);

  or or_1 (Q7, D7, C7, B7, A7);
  or or_2 (Q6, C6, D6, B6, A6);
  or or_3 (Q5, D5, C5, B5, A5);
  or or_4 (Q4, C4, D4, B4, A4);
  or or_5 (Q3, D3, C3, B3, A3);
  or or_6 (Q2, C2, D2, B2, A2);
  or or_7 (Q1, D1, C1, B1, A1);
  or or_8 (Q0, C0, D0, B0, A0);
endmodule

module rising_edge_D_flip_flop (
  input  D,
  input  enable,
  output Q,
  output Q_prime
);

  wire nand_1_out, nand_2_out, nand_3_out, nand_4_out;

  nand nand_1 (nand_1_out, nand_4_out, nand_2_out);
  nand nand_2 (nand_2_out, nand_1_out, enable);
  nand nand_3 (nand_3_out, nand_2_out, enable, nand_4_out);
  nand nand_4 (nand_4_out, nand_3_out, D);
  nand nand_5 (Q, nand_2_out, Q_prime);
  nand nand_6 (Q_prime, Q, nand_3_out);
endmodule

module falling_edge_D_flip_flop (
  input  D,
  input  enable,
  output Q,
  output Q_prime
);

  wire nand_1_out, nand_2_out, nand_3_out, nand_4_out, not_1_out;

  not not_1 (not_1_out, enable);
  nand nand_1 (nand_1_out, nand_4_out, nand_2_out);
  nand nand_2 (nand_2_out, nand_1_out, not_1_out);
  nand nand_3 (nand_3_out, nand_2_out, not_1_out, nand_4_out);
  nand nand_4 (nand_4_out, nand_3_out, D);
  nand nand_5 (Q, nand_2_out, Q_prime);
  nand nand_6 (Q_prime, Q, nand_3_out);
endmodule

module falling_edge_register (
  input  A0,
  input  A1,
  input  A2,
  input  A3,
  input  A4,
  input  A5,
  input  A6,
  input  A7,
  input  enable,
  input  read,
  output Q0,
  output Q1,
  output Q2,
  output Q3,
  output Q4,
  output Q5,
  output Q6,
  output Q7
);

  wire d_ff_1_q, d_ff_2_q, d_ff_3_q, d_ff_4_q, d_ff_5_q, d_ff_6_q, d_ff_7_q, d_ff_8_q, not_1_out;

  D_Flip_Flop d_ff_1 (.clk(not_1_out), .D(A0), .Q(d_ff_1_q));  // open: Qn, preset, en, reset
  D_Flip_Flop d_ff_2 (.clk(not_1_out), .D(A1), .Q(d_ff_2_q));  // open: Qn, preset, en, reset
  D_Flip_Flop d_ff_3 (.clk(not_1_out), .D(A2), .Q(d_ff_3_q));  // open: Qn, preset, en, reset
  D_Flip_Flop d_ff_4 (.clk(not_1_out), .D(A3), .Q(d_ff_4_q));  // open: Qn, preset, en, reset
  D_Flip_Flop d_ff_5 (.clk(not_1_out), .D(A4), .Q(d_ff_5_q));  // open: Qn, preset, en, reset
  D_Flip_Flop d_ff_6 (.clk(not_1_out), .D(A5), .Q(d_ff_6_q));  // open: Qn, preset, en, reset
  D_Flip_Flop d_ff_7 (.clk(not_1_out), .D(A6), .Q(d_ff_7_q));  // open: Qn, preset, en, reset
  D_Flip_Flop d_ff_8 (.clk(not_1_out), .D(A7), .Q(d_ff_8_q));  // open: Qn, preset, en, reset
  not not_1 (not_1_out, enable);
  and and_1 (Q0, d_ff_1_q, read);
  and and_2 (Q1, d_ff_2_q, read);
  and and_3 (Q2, d_ff_3_q, read);
  and and_4 (Q3, d_ff_4_q, read);
  and and_5 (Q4, d_ff_5_q, read);
  and and_6 (Q5, d_ff_6_q, read);
  and and_7 (Q6, d_ff_7_q, read);
  and and_8 (Q7, d_ff_8_q, read);
endmodule

module rising_edge_register (
  input  A0,
  input  A1,
  input  A2,
  input  A3,
  input  A4,
  input  A5,
  input  A6,
  input  A7,
  input  write,
  input  read,
  output Q0,
  output Q1,
  output Q2,
  output Q3,
  output Q4,
  output Q5,
  output Q6,
  output Q7
);

  wire rising_edge_d_flip_flop_1_q, rising_edge_d_flip_flop_2_q, rising_edge_d_flip_flop_3_q,
       rising_edge_d_flip_flop_4_q, rising_edge_d_flip_flop_5_q, rising_edge_d_flip_flop_6_q,
       rising_edge_d_flip_flop_7_q, rising_edge_d_flip_flop_8_q;

  rising_edge_D_flip_flop rising_edge_d_flip_flop_1 (
    .D(A0), .enable(write), .Q(rising_edge_d_flip_flop_1_q));  // open: Q_prime
  rising_edge_D_flip_flop rising_edge_d_flip_flop_2 (
    .D(A1), .enable(write), .Q(rising_edge_d_flip_flop_2_q));  // open: Q_prime
  rising_edge_D_flip_flop rising_edge_d_flip_flop_3 (
    .D(A2), .enable(write), .Q(rising_edge_d_flip_flop_3_q));  // open: Q_prime
  rising_edge_D_flip_flop rising_edge_d_flip_flop_4 (
    .D(A3), .enable(write), .Q(rising_edge_d_flip_flop_4_q));  // open: Q_prime
  rising_edge_D_flip_flop rising_edge_d_flip_flop_5 (
    .D(A4), .enable(write), .Q(rising_edge_d_flip_flop_5_q));  // open: Q_prime
  rising_edge_D_flip_flop rising_edge_d_flip_flop_6 (
    .D(A5), .enable(write), .Q(rising_edge_d_flip_flop_6_q));  // open: Q_prime
  rising_edge_D_flip_flop rising_edge_d_flip_flop_7 (
    .D(A6), .enable(write), .Q(rising_edge_d_flip_flop_7_q));  // open: Q_prime
  rising_edge_D_flip_flop rising_edge_d_flip_flop_8 (
    .D(A7), .enable(write), .Q(rising_edge_d_flip_flop_8_q));  // open: Q_prime
  and and_1 (Q0, rising_edge_d_flip_flop_1_q, read);
  and and_2 (Q1, rising_edge_d_flip_flop_2_q, read);
  and and_3 (Q2, rising_edge_d_flip_flop_3_q, read);
  and and_4 (Q3, rising_edge_d_flip_flop_4_q, read);
  and and_5 (Q4, rising_edge_d_flip_flop_5_q, read);
  and and_6 (Q5, rising_edge_d_flip_flop_6_q, read);
  and and_7 (Q6, rising_edge_d_flip_flop_7_q, read);
  and and_8 (Q7, rising_edge_d_flip_flop_8_q, read);
endmodule

module _24_8_MUX (
  input  C7,
  input  C6,
  input  C5,
  input  C4,
  input  C3,
  input  C2,
  input  C1,
  input  C0,
  input  B7,
  input  B6,
  input  B5,
  input  B4,
  input  B3,
  input  B2,
  input  B1,
  input  B0,
  input  A7,
  input  A6,
  input  A5,
  input  A4,
  input  A3,
  input  A2,
  input  A1,
  input  A0,
  input  cntl2,
  input  cntl1,
  input  cntl0,
  output Q7,
  output Q6,
  output Q5,
  output Q4,
  output Q3,
  output Q2,
  output Q1,
  output Q0
);

  wire and_1_out, and_2_out, and_3_out, and_4_out, and_5_out, and_6_out, and_7_out, and_8_out, and_9_out,
       and_10_out, and_11_out, and_12_out, and_13_out, and_14_out, and_15_out, and_16_out, and_17_out,
       and_18_out, and_19_out, and_20_out, and_21_out, and_22_out, and_23_out, and_24_out;

  and and_1 (and_1_out, C7, cntl2);
  and and_2 (and_2_out, A7, cntl0);
  and and_3 (and_3_out, B7, cntl1);
  or or_1 (Q7, and_1_out, and_3_out, and_2_out);
  and and_4 (and_4_out, C6, cntl2);
  and and_5 (and_5_out, A6, cntl0);
  and and_6 (and_6_out, B6, cntl1);
  or or_2 (Q6, and_4_out, and_6_out, and_5_out);
  and and_7 (and_7_out, B5, cntl1);
  and and_8 (and_8_out, C5, cntl2);
  or or_3 (Q5, and_8_out, and_7_out, and_10_out);
  and and_9 (and_9_out, C4, cntl2);
  and and_10 (and_10_out, A5, cntl0);
  and and_11 (and_11_out, A4, cntl0);
  and and_12 (and_12_out, C3, cntl2);
  and and_13 (and_13_out, B4, cntl1);
  or or_4 (Q4, and_9_out, and_13_out, and_11_out);
  and and_14 (and_14_out, B3, cntl1);
  and and_15 (and_15_out, A3, cntl0);
  or or_5 (Q3, and_12_out, and_14_out, and_15_out);
  and and_16 (and_16_out, B2, cntl1);
  and and_17 (and_17_out, A2, cntl0);
  and and_18 (and_18_out, C2, cntl2);
  or or_6 (Q2, and_18_out, and_16_out, and_17_out);
  and and_19 (and_19_out, C1, cntl2);
  and and_20 (and_20_out, B1, cntl1);
  or or_7 (Q1, and_19_out, and_20_out, and_22_out);
  and and_21 (and_21_out, C0, cntl2);
  and and_22 (and_22_out, A1, cntl0);
  and and_23 (and_23_out, B0, cntl1);
  and and_24 (and_24_out, A0, cntl0);
  or or_8 (Q0, and_21_out, and_23_out, and_24_out);
endmodule

module _8_24_DEMUX (
  input  A7,
  input  A6,
  input  A5,
  input  A4,
  input  A3,
  input  A2,
  input  A1,
  input  A0,
  input  cntl2,
  input  cntl1,
  input  cntl0,
  output Q27,
  output Q26,
  output Q25,
  output Q24,
  output Q23,
  output Q22,
  output Q21,
  output Q20,
  output Q17,
  output Q16,
  output Q15,
  output Q14,
  output Q13,
  output Q12,
  output Q11,
  output Q10,
  output Q07,
  output Q06,
  output Q05,
  output Q04,
  output Q03,
  output Q02,
  output Q01,
  output Q00
);

  and and_1 (Q26, A6, cntl2);
  and and_2 (Q25, A5, cntl2);
  and and_3 (Q27, A7, cntl2);
  and and_4 (Q23, A3, cntl2);
  and and_5 (Q22, A2, cntl2);
  and and_6 (Q24, A4, cntl2);
  and and_7 (Q21, A1, cntl2);
  and and_8 (Q20, A0, cntl2);
  and and_9 (Q16, A6, cntl1);
  and and_10 (Q17, A7, cntl1);
  and and_11 (Q14, A4, cntl1);
  and and_12 (Q13, A3, cntl1);
  and and_13 (Q15, A5, cntl1);
  and and_14 (Q11, A1, cntl1);
  and and_15 (Q12, A2, cntl1);
  and and_16 (Q10, A0, cntl1);
  and and_17 (Q06, A6, cntl0);
  and and_18 (Q07, A7, cntl0);
  and and_19 (Q05, A5, cntl0);
  and and_20 (Q04, A4, cntl0);
  and and_21 (Q02, A2, cntl0);
  and and_22 (Q03, A3, cntl0);
  and and_23 (Q01, A1, cntl0);
  and and_24 (Q00, A0, cntl0);
endmodule

module _8_16_DEMUX (
  input  A7,
  input  A6,
  input  A5,
  input  A4,
  input  A3,
  input  A2,
  input  A1,
  input  A0,
  input  cntl1,
  input  cntl0,
  output Q17,
  output Q16,
  output Q15,
  output Q14,
  output Q13,
  output Q12,
  output Q11,
  output Q10,
  output Q07,
  output Q06,
  output Q05,
  output Q04,
  output Q03,
  output Q02,
  output Q01,
  output Q00
);

  and and_1 (Q17, A7, cntl1);
  and and_2 (Q14, A4, cntl1);
  and and_3 (Q15, A5, cntl1);
  and and_4 (Q16, A6, cntl1);
  and and_5 (Q13, A3, cntl1);
  and and_6 (Q11, A1, cntl1);
  and and_7 (Q12, A2, cntl1);
  and and_8 (Q10, A0, cntl1);
  and and_9 (Q07, A7, cntl0);
  and and_10 (Q05, A5, cntl0);
  and and_11 (Q06, A6, cntl0);
  and and_12 (Q04, A4, cntl0);
  and and_13 (Q03, A3, cntl0);
  and and_14 (Q02, A2, cntl0);
  and and_15 (Q01, A1, cntl0);
  and and_16 (Q00, A0, cntl0);
endmodule

module _16_8_MUX (
  input  B7,
  input  B6,
  input  B5,
  input  B4,
  input  B3,
  input  B2,
  input  B1,
  input  B0,
  input  A7,
  input  A6,
  input  A5,
  input  A4,
  input  A3,
  input  A2,
  input  A1,
  input  A0,
  input  cntl1,
  input  cntl0,
  output Q7,
  output Q6,
  output Q5,
  output Q4,
  output Q3,
  output Q2,
  output Q1,
  output Q0
);

  wire and_1_out, and_2_out, and_3_out, and_4_out, and_5_out, and_6_out, and_7_out, and_8_out, and_9_out,
       and_10_out, and_11_out, and_12_out, and_13_out, and_14_out, and_15_out, and_16_out;

  and and_1 (and_1_out, A7, cntl0);
  and and_2 (and_2_out, B7, cntl1);
  or or_1 (Q7, and_2_out, and_1_out);
  and and_3 (and_3_out, A6, cntl0);
  and and_4 (and_4_out, B6, cntl1);
  or or_2 (Q6, and_4_out, and_3_out);
  and and_5 (and_5_out, B5, cntl1);
  and and_6 (and_6_out, A5, cntl0);
  or or_3 (Q5, and_5_out, and_6_out);
  and and_7 (and_7_out, A4, cntl0);
  and and_8 (and_8_out, B4, cntl1);
  or or_4 (Q4, and_8_out, and_7_out);
  and and_9 (and_9_out, B3, cntl1);
  and and_10 (and_10_out, A3, cntl0);
  and and_11 (and_11_out, B2, cntl1);
  or or_5 (Q3, and_9_out, and_10_out);
  and and_12 (and_12_out, B1, cntl1);
  and and_13 (and_13_out, A2, cntl0);
  or or_6 (Q2, and_11_out, and_13_out);
  and and_14 (and_14_out, B0, cntl1);
  and and_15 (and_15_out, A1, cntl0);
  or or_7 (Q1, and_12_out, and_15_out);
  or or_8 (Q0, and_14_out, and_16_out);
  and and_16 (and_16_out, A0, cntl0);
endmodule

module _3_1_MUX_8_bit (
  input  [7:0] C,
  input  [7:0] B,
  input  [7:0] A,
  input  cntl2,
  input  cntl1,
  input  cntl0,
  output [7:0] Q
);

  wire and_1_out, and_2_out, and_3_out, and_4_out, and_5_out, and_6_out, and_7_out, and_8_out, and_9_out,
       and_10_out, and_11_out, and_12_out, and_13_out, and_14_out, and_15_out, and_16_out, and_17_out,
       and_18_out, and_19_out, and_20_out, and_21_out, and_22_out, and_23_out, and_24_out;

  and and_1 (and_1_out, C[7], cntl2);
  and and_2 (and_2_out, A[7], cntl0);
  and and_3 (and_3_out, B[7], cntl1);
  or or_1 (Q[7], and_1_out, and_3_out, and_2_out);
  and and_4 (and_4_out, B[6], cntl1);
  and and_5 (and_5_out, A[6], cntl0);
  and and_6 (and_6_out, C[6], cntl2);
  or or_2 (Q[6], and_6_out, and_4_out, and_5_out);
  and and_7 (and_7_out, B[5], cntl1);
  and and_8 (and_8_out, C[5], cntl2);
  or or_3 (Q[5], and_8_out, and_7_out, and_9_out);
  and and_9 (and_9_out, A[5], cntl0);
  and and_10 (and_10_out, C[4], cntl2);
  and and_11 (and_11_out, A[4], cntl0);
  and and_12 (and_12_out, C[3], cntl2);
  and and_13 (and_13_out, B[4], cntl1);
  or or_4 (Q[4], and_10_out, and_13_out, and_11_out);
  and and_14 (and_14_out, A[3], cntl0);
  and and_15 (and_15_out, B[3], cntl1);
  or or_5 (Q[3], and_12_out, and_15_out, and_14_out);
  and and_16 (and_16_out, C[2], cntl2);
  and and_17 (and_17_out, A[2], cntl0);
  and and_18 (and_18_out, B[2], cntl1);
  or or_6 (Q[2], and_16_out, and_18_out, and_17_out);
  and and_19 (and_19_out, C[1], cntl2);
  and and_20 (and_20_out, B[1], cntl1);
  or or_7 (Q[1], and_19_out, and_20_out, and_21_out);
  and and_21 (and_21_out, A[1], cntl0);
  and and_22 (and_22_out, C[0], cntl2);
  and and_23 (and_23_out, B[0], cntl1);
  and and_24 (and_24_out, A[0], cntl0);
  or or_8 (Q[0], and_22_out, and_23_out, and_24_out);
endmodule

module _1_3_MUX_8_bit (
  input  [7:0] A,
  input  cntl2,
  input  cntl1,
  input  cntl0,
  output [7:0] Q2,
  output [7:0] Q1,
  output [7:0] Q0
);

  and and_1 (Q2[5], A[5], cntl2);
  and and_2 (Q2[6], A[6], cntl2);
  and and_3 (Q2[7], A[7], cntl2);
  and and_4 (Q2[3], A[3], cntl2);
  and and_5 (Q2[4], A[4], cntl2);
  and and_6 (Q2[2], A[2], cntl2);
  and and_7 (Q2[0], A[0], cntl2);
  and and_8 (Q2[1], A[1], cntl2);
  and and_9 (Q1[6], A[6], cntl1);
  and and_10 (Q1[7], A[7], cntl1);
  and and_11 (Q1[3], A[3], cntl1);
  and and_12 (Q1[4], A[4], cntl1);
  and and_13 (Q1[5], A[5], cntl1);
  and and_14 (Q1[0], A[0], cntl1);
  and and_15 (Q1[2], A[2], cntl1);
  and and_16 (Q1[1], A[1], cntl1);
  and and_17 (Q0[7], A[7], cntl0);
  and and_18 (Q0[6], A[6], cntl0);
  and and_19 (Q0[4], A[4], cntl0);
  and and_20 (Q0[5], A[5], cntl0);
  and and_21 (Q0[3], A[3], cntl0);
  and and_22 (Q0[1], A[1], cntl0);
  and and_23 (Q0[2], A[2], cntl0);
  and and_24 (Q0[0], A[0], cntl0);
endmodule

module _1_of_8_decoder (
  input  A2,
  input  A1,
  input  A0,
  output Q7,
  output Q6,
  output Q5,
  output Q4,
  output Q3,
  output Q2,
  output Q1,
  output Q0
);

  wire not_1_out, not_2_out, not_3_out;

  not not_1 (not_1_out, A2);
  and and_1 (Q7, A2, A1, A0);
  not not_2 (not_2_out, A1);
  and and_2 (Q5, A2, not_2_out, A0);
  and and_3 (Q6, A2, A1, not_3_out);
  and and_4 (Q3, not_1_out, A1, A0);
  and and_5 (Q2, not_1_out, A1, not_3_out);
  and and_6 (Q4, A2, not_2_out, not_3_out);
  not not_3 (not_3_out, A0);
  and and_7 (Q0, not_1_out, not_2_out, not_3_out);
  and and_8 (Q1, not_1_out, not_2_out, A0);
endmodule

module _3_1_MUX (
  input  A2,
  input  A1,
  input  A0,
  input  cntl0,
  input  cnt1,
  input  cntl2,
  output Q
);

  wire and_1_out, and_2_out, and_3_out;

  and and_1 (and_1_out, A2, cntl2);
  and and_2 (and_2_out, A0, cntl0);
  and and_3 (and_3_out, A1, cnt1);
  or or_1 (Q, and_1_out, and_3_out, and_2_out);
endmodule

module _4_2_encoder (
  input  A3,
  input  A2,
  input  A1,
  input  A0,
  output Q1,
  output Q0
);

  wire not_1_out, not_2_out;

  not not_1 (not_1_out, A1);
  and and_1 (Q1, not_1_out, not_2_out);
  or or_1 (Q0, A3, A1);
  not not_2 (not_2_out, A0);
endmodule

module _5_3_priority_encoder (
  input  A4,
  input  A3,
  input  A2,
  input  A1,
  input  A0,
  output Q2,
  output Q0,
  output Q1
);

  wire and_1_out, and_2_out, and_3_out, and_4_out, not_1_out, not_2_out;

  not not_1 (not_1_out, A4);
  not not_2 (not_2_out, A2);
  and and_1 (and_1_out, not_1_out, A2);
  and and_2 (and_2_out, A3, not_1_out);
  or or_1 (Q1, and_2_out, and_1_out);
  and and_3 (and_3_out, A3, not_1_out);
  and and_4 (and_4_out, not_1_out, not_2_out, A1);
  or or_2 (Q0, and_3_out, and_4_out);

  assign Q2 = A4;
endmodule

module _8_to_3_priority_encoder (
  input  A7,
  input  A6,
  input  A5,
  input  A4,
  input  A3,
  input  A2,
  input  A1,
  input  A0,
  output Q2,
  output Q1,
  output Q0
);

  wire controlled_buffer_1_out, controlled_buffer_2_out, not_1_out, not_2_out;

  or or_1 (Q2, A7, A6, A5, A4);
  not not_1 (not_1_out, A5);
  or or_2 (Q1, A7, A6, A3, A2);
  not not_2 (not_2_out, A2);
  or or_3 (Q0, A7, A5, A3, controlled_buffer_2_out);
  assign controlled_buffer_1_out = not_2_out ? A1 : 1'bz;  // Controlled_Buffer controlled_buffer_1
  assign controlled_buffer_2_out = not_1_out ? controlled_buffer_1_out : 1'bz;  // Controlled_Buffer controlled_buffer_2
endmodule
