// Logisim project OZ-2.circ as structural Verilog: 11 circuits, main circuit OZ-2
module OZ_2 (
  input  PN0,
  input  PN1,
  input  PN2,
  input  PN3,
  input  PN4,
  input  PN5,
  input  PN6,
  input  PN7,
  input  CLK,
  input  [15:0] IP1,
  input  [15:0] IP2,
  input  [7:0] A,
  input  [7:0] A_2,
  input  [7:0] A_3,
  input  [7:0] A_4,
  output [15:0] OP1,
  output [15:0] OP2,
  output OPN0,
  output OPN1,
  output OPN2,
  output OPN3,
  output OPN4,
  output OPN5,
  output OPN6,
  output OPN7
);

  wire alu_1_c, alu_1_nz, alu_1_s, alu_1_z, condition_block_1_true, input_pin_controller_1_f,
       input_pin_controller_1_n, instruction_decoder_1_alu_cntl0, instruction_decoder_1_alu_cntl1,
       instruction_decoder_1_alu_cntl2, instruction_decoder_1_alu_instruction, instruction_decoder_1_alu_s_a,
       instruction_decoder_1_iprt_is_rec, instruction_decoder_1_iprt_is_send, instruction_decoder_1_iprt_rd,
       instruction_decoder_1_iprt_sel, instruction_decoder_1_oprt_sel__rec,
       instruction_decoder_1_oprt_wrt__rec, instruction_decoder_1_pc_instruction,
       instruction_decoder_1_pon_poff, instruction_decoder_1_pon_poff_instruction,
       instruction_decoder_1_ram_rd, instruction_decoder_1_ram_wrt, instruction_decoder_1_reg_is_rec,
       instruction_decoder_1_reg_is_send, instruction_decoder_1_reg_rd___send,
       instruction_decoder_1_reg_rd__rec, instruction_decoder_1_reg_wrt__rec,
       instruction_decoder_1_uip_instruction, instruction_decoder_1_uiprt_instruction;
  wire [1:0] instruction_decoder_1_register_address__rec, instruction_decoder_1_register_address__send;
  wire [2:0] instruction_decoder_1_bus_out_cntl__rec, instruction_decoder_1_bus_out_cntl__send,
       instruction_decoder_1_pin_number, instruction_decoder_1_ram_bus_cntl;
  wire [6:0] instruction_decoder_1_test_s_6;
  wire [15:0] input_port_controller_1_to_alu_a_bus, input_port_controller_1_to_alu_b_bus,
       input_port_controller_1_to_oprt_bus, input_port_controller_1_to_ram_adr__bus,
       input_port_controller_1_to_ram_data_bus, input_port_controller_1_to_register_bus;

  Input_Port_Controller input_port_controller_1 (
    .P1_15(IP1[15]), .P1_14(IP1[14]), .P1_13(IP1[13]), .P1_12(IP1[12]), .P1_11(IP1[11]), .P1_10(IP1[10]),
    .P1_9(IP1[9]), .P1_8(IP1[8]), .P1_7(IP1[7]), .P1_6(IP1[6]), .P1_5(IP1[5]), .P1_4(IP1[4]), .P1_3(IP1[3]),
    .P1_2(IP1[2]), .P1_1(IP1[1]), .P1_0(IP1[0]), .P2_15(IP2[15]), .P2_14(IP2[14]), .P2_13(IP2[13]),
    .P2_12(IP2[12]), .P2_11(IP2[11]), .P2_10(IP2[10]), .P2_9(IP2[9]), .P2_8(IP2[8]), .P2_7(IP2[7]),
    .P2_6(IP2[6]), .P2_5(IP2[5]), .P2_4(IP2[4]), .P2_3(IP2[3]), .P2_2(IP2[2]), .P2_1(IP2[1]), .P2_0(IP2[0]),
    .to_oprt_bus(input_port_controller_1_to_oprt_bus),
    .to_Register_bus(input_port_controller_1_to_register_bus),
    .to_RAM_adr__bus(input_port_controller_1_to_ram_adr__bus),
    .to_ALU_B_bus(input_port_controller_1_to_alu_b_bus), .to_ALU_A_bus(input_port_controller_1_to_alu_a_bus),
    .to_RAM_data_bus(input_port_controller_1_to_ram_data_bus), .CLK(CLK),
    .Condition_Block_in(condition_block_1_true), .Read(instruction_decoder_1_iprt_rd),
    .Update(instruction_decoder_1_uiprt_instruction), .Port_Select(instruction_decoder_1_iprt_sel),
    .bus_cntl__rec(instruction_decoder_1_bus_out_cntl__rec),
    .bus_cntl__send(instruction_decoder_1_bus_out_cntl__send),
    .iprt_is_rec(instruction_decoder_1_iprt_is_rec), .iprt_is_send(instruction_decoder_1_iprt_is_send));
  Output_Port_Controller output_port_controller_1 (
    .Output_Port_Data_Bus(input_port_controller_1_to_oprt_bus), .OP1_15(OP1[15]), .OP1_14(OP1[14]),
    .OP1_13(OP1[13]), .OP1_12(OP1[12]), .OP1_11(OP1[11]), .OP1_10(OP1[10]), .OP1_9(OP1[9]), .OP1_8(OP1[8]),
    .OP1_7(OP1[7]), .OP1_6(OP1[6]), .OP1_5(OP1[5]), .OP1_4(OP1[4]), .OP1_3(OP1[3]), .OP1_2(OP1[2]),
    .OP1_1(OP1[1]), .OP1_0(OP1[0]), .OP2_15(OP2[15]), .OP2_14(OP2[14]), .OP2_13(OP2[13]), .OP2_12(OP2[12]),
    .OP2_11(OP2[11]), .OP2_10(OP2[10]), .OP2_9(OP2[9]), .OP2_8(OP2[8]), .OP2_7(OP2[7]), .OP2_6(OP2[6]),
    .OP2_5(OP2[5]), .OP2_4(OP2[4]), .OP2_3(OP2[3]), .OP2_2(OP2[2]), .OP2_1(OP2[1]), .OP2_0(OP2[0]),
    .CLK(CLK), .Condition_Block(condition_block_1_true), .Write(instruction_decoder_1_oprt_wrt__rec),
    .Port_Select(instruction_decoder_1_oprt_sel__rec));
  Register_File register_file_1 (
    .Register_Data_Bus_in(input_port_controller_1_to_register_bus),
    .to_oprt_bus(input_port_controller_1_to_oprt_bus),
    .to_Register_bus(input_port_controller_1_to_register_bus),
    .to_RAM_adr__bus(input_port_controller_1_to_ram_adr__bus),
    .to_ALU_B_bus(input_port_controller_1_to_alu_b_bus), .to_ALU_A_bus(input_port_controller_1_to_alu_a_bus),
    .to_oprt_bus_2(input_port_controller_1_to_oprt_bus),
    .to_Register_bus_2(input_port_controller_1_to_register_bus),
    .to_RAM_adr__bus_2(input_port_controller_1_to_ram_adr__bus),
    .to_ALU_B_bus_2(input_port_controller_1_to_alu_b_bus),
    .to_ALU_A_bus_2(input_port_controller_1_to_alu_a_bus),
    .to_RAM_data_bus(input_port_controller_1_to_ram_data_bus),
    .ALU_instruction_signifier_in(instruction_decoder_1_alu_instruction), .CLK(CLK),
    .Condition_Block_in(condition_block_1_true), .Read__rec(instruction_decoder_1_reg_rd__rec),
    .Write__rec(instruction_decoder_1_reg_wrt__rec),
    .Address__rec(instruction_decoder_1_register_address__rec),
    .Bus_out_cntl__rec(instruction_decoder_1_bus_out_cntl__rec),
    .Read__send(instruction_decoder_1_reg_rd___send),
    .Address__send(instruction_decoder_1_register_address__send),
    .Bus_out_cntl__send(instruction_decoder_1_bus_out_cntl__send),
    .Register_is_rec__sig(instruction_decoder_1_reg_is_rec),
    .Register_is_send_sig(instruction_decoder_1_reg_is_send));
  Output_Pin_Controller output_pin_controller_1 (
    .Pin_Number(instruction_decoder_1_pin_number), .OPN7(OPN0), .OPN6(OPN1), .OPN5(OPN2), .OPN4(OPN3),
    .OPN3(OPN4), .OPN2(OPN5), .OPN1(OPN6), .OPN0(OPN7), .CLK(CLK), .Condition_Block(condition_block_1_true),
    .Write(instruction_decoder_1_pon_poff_instruction), .Pin_on_off_selection(instruction_decoder_1_pon_poff));
  RAM ram_1 (
    .RAM_Address_bus_in(input_port_controller_1_to_ram_adr__bus),
    .RAM_Data_bus_in(input_port_controller_1_to_ram_data_bus),
    .to_oprt_bus(input_port_controller_1_to_oprt_bus),
    .to_Register_bus(input_port_controller_1_to_register_bus),
    .to_ALU_B_bus(input_port_controller_1_to_alu_b_bus), .to_ALU_A_bus(input_port_controller_1_to_alu_a_bus),
    .CLK(CLK), .Condition_Block_in(condition_block_1_true), .Read(instruction_decoder_1_ram_rd),
    .Write(instruction_decoder_1_ram_wrt), .bus_out_cntl(instruction_decoder_1_ram_bus_cntl));
  ALU alu_1 (
    .B(input_port_controller_1_to_alu_b_bus), .A(input_port_controller_1_to_alu_a_bus), .S(alu_1_s),
    .C(alu_1_c), .NZ(alu_1_nz), .Z(alu_1_z), .Q(input_port_controller_1_to_register_bus),
    .SUB_ADD(instruction_decoder_1_alu_s_a), .cntl2(instruction_decoder_1_alu_cntl2),
    .cntl1(instruction_decoder_1_alu_cntl1), .cntl0(instruction_decoder_1_alu_cntl0), .CLK(CLK),
    .ALU_op__sig__in(instruction_decoder_1_alu_instruction));
  Instruction_Decoder instruction_decoder_1 (
    .reg_wrt__rec(instruction_decoder_1_reg_wrt__rec), .reg_rd__rec(instruction_decoder_1_reg_rd__rec),
    .register_address__rec(instruction_decoder_1_register_address__rec),
    .oprt_wrt__rec(instruction_decoder_1_oprt_wrt__rec), .oprt_sel__rec(instruction_decoder_1_oprt_sel__rec),
    .iprt_rd(instruction_decoder_1_iprt_rd), .iprt_sel(instruction_decoder_1_iprt_sel),
    .bus_out_cntl__rec(instruction_decoder_1_bus_out_cntl__rec),
    .reg_rd___send(instruction_decoder_1_reg_rd___send),
    .register_address__send(instruction_decoder_1_register_address__send),
    .bus_out_cntl__send(instruction_decoder_1_bus_out_cntl__send),
    .RAM_bus_cntl(instruction_decoder_1_ram_bus_cntl), .RAM_rd(instruction_decoder_1_ram_rd),
    .RAM_wrt(instruction_decoder_1_ram_wrt), .A31(A[7]), .A30(A[6]), .A29(A[5]), .A28(A[4]), .A27(A[3]),
    .A26(A[2]), .A25(A[1]), .A24(A[0]), .A23(A_2[7]), .A22(A_2[6]), .A21(A_2[5]), .A20(A_2[4]), .A19(A_2[3]),
    .A18(A_2[2]), .A17(A_2[1]), .A16(A_2[0]), .A15(A_3[7]), .A14(A_3[6]), .A13(A_3[5]), .A12(A_3[4]),
    .A11(A_3[3]), .A10(A_3[2]), .A9(A_3[1]), .A8(A_3[0]), .A7(A_4[7]), .A6(A_4[6]), .A5(A_4[5]), .A4(A_4[4]),
    .A3(A_4[3]), .A2(A_4[2]), .A1(A_4[1]), .A0(A_4[0]), .to_oprt_bus(input_port_controller_1_to_oprt_bus),
    .to_Register_bus(input_port_controller_1_to_register_bus),
    .to_RAM_adr__bus(input_port_controller_1_to_ram_adr__bus),
    .to_ALU_B_bus(input_port_controller_1_to_alu_b_bus), .to_ALU_A_bus(input_port_controller_1_to_alu_a_bus),
    .to_RAM_data_bus(input_port_controller_1_to_ram_data_bus),
    .Cndt_prime_l_Inst(instruction_decoder_1_test_s_6[6]), .Test_S(instruction_decoder_1_test_s_6[5]),
    .Test_S_2(instruction_decoder_1_test_s_6[4]), .Test_S_3(instruction_decoder_1_test_s_6[3]),
    .Test_S_4(instruction_decoder_1_test_s_6[2]), .Test_S_5(instruction_decoder_1_test_s_6[1]),
    .Test_S_6(instruction_decoder_1_test_s_6[0]), .ALU_cntl2(instruction_decoder_1_alu_cntl2),
    .ALU_cntl1(instruction_decoder_1_alu_cntl1), .ALU_cntl0(instruction_decoder_1_alu_cntl0),
    .ALU_S_A(instruction_decoder_1_alu_s_a), .PON_POFF(instruction_decoder_1_pon_poff),
    .ALU_instruction(instruction_decoder_1_alu_instruction), .Pin_Number(instruction_decoder_1_pin_number),
    .PON_POFF_instruction(instruction_decoder_1_pon_poff_instruction),
    .PC_instruction(instruction_decoder_1_pc_instruction),
    .UIP_instruction(instruction_decoder_1_uip_instruction),
    .UIPRT_instruction(instruction_decoder_1_uiprt_instruction),
    .reg_is_rec(instruction_decoder_1_reg_is_rec), .reg_is_send(instruction_decoder_1_reg_is_send),
    .iprt_is_rec(instruction_decoder_1_iprt_is_rec), .iprt_is_send(instruction_decoder_1_iprt_is_send));  // open: to_P_C__Control, JP_instruction, CP_instruction, oprt_is_rec
  Input_Pin_Controller input_pin_controller_1 (
    .Pin_Number(instruction_decoder_1_pin_number), .CLK(CLK), .Condition_Block_in(condition_block_1_true),
    .Check_Pin(instruction_decoder_1_pc_instruction), .Update_Pins(instruction_decoder_1_uip_instruction),
    .A0(PN0), .A1(PN1), .A2(PN2), .A3(PN3), .A4(PN4), .A5(PN5), .A6(PN6), .A7(PN7),
    .N(input_pin_controller_1_n), .F(input_pin_controller_1_f));
  Condition_Block condition_block_1 (
    .Testing(instruction_decoder_1_test_s_6[6]), .Test_S(instruction_decoder_1_test_s_6[5]),
    .Test_C(instruction_decoder_1_test_s_6[4]), .Test_NZ(instruction_decoder_1_test_s_6[3]),
    .Test_Z(instruction_decoder_1_test_s_6[2]), .Test_N(instruction_decoder_1_test_s_6[1]),
    .Test_F(instruction_decoder_1_test_s_6[0]), .S(alu_1_s), .C(alu_1_c), .NZ(alu_1_nz), .Z(alu_1_z),
    .N(input_pin_controller_1_n), .F(input_pin_controller_1_f), .True(condition_block_1_true));

  // Notes on the sheet:
  //   Input Port Controller
  //   Output Port Controller
  //   Register File
  //   Output Pin cntl
  //   RAM
  //   Instruction Decoder
  //   ALU
  //   Input Pin Cntl
  //   Condition
  //   Block
endmodule

module Instruction_Decoder (
  input  A31,
  input  A30,
  input  A29,
  input  A28,
  input  A27,
  input  A26,
  input  A25,
  input  A24,
  input  A23,
  input  A22,
  input  A21,
  input  A20,
  input  A19,
  input  A18,
  input  A17,
  input  A16,
  input  A15,
  input  A14,
  input  A13,
  input  A12,
  input  A11,
  input  A10,
  input  A9,
  input  A8,
  input  A7,
  input  A6,
  input  A5,
  input  A4,
  input  A3,
  input  A2,
  input  A1,
  input  A0,
  output ALU_cntl2,
  output ALU_cntl1,
  output reg_wrt__rec,
  output ALU_cntl0,
  output reg_rd__rec,
  output ALU_S_A,
  output PON_POFF,
  output [1:0] register_address__rec,
  output ALU_instruction,
  output [2:0] Pin_Number,
  output oprt_wrt__rec,
  output JP_instruction,
  output oprt_sel__rec,
  output CP_instruction,
  output iprt_rd,
  output PON_POFF_instruction,
  output iprt_sel,
  output PC_instruction,
  output UIP_instruction,
  output UIPRT_instruction,
  output [2:0] bus_out_cntl__rec,
  output Cndt_prime_l_Inst,
  output Test_S,
  output Test_S_2,
  output Test_S_3,
  output Test_S_4,
  output Test_S_5,
  output Test_S_6,
  output [15:0] to_oprt_bus,
  output [15:0] to_Register_bus,
  output [15:0] to_RAM_adr__bus,
  output [15:0] to_ALU_B_bus,
  output [15:0] to_ALU_A_bus,
  output [15:0] to_RAM_data_bus,
  output [15:0] to_P_C__Control,
  output reg_rd___send,
  output reg_is_rec,
  output [1:0] register_address__send,
  output reg_is_send,
  output iprt_is_rec,
  output iprt_is_send,
  output oprt_is_rec,
  output [2:0] bus_out_cntl__send,
  output [2:0] RAM_bus_cntl,
  output RAM_rd,
  output RAM_wrt
);

  wire and_1_out, and_2_out, and_3_out, and_5_out, and_6_out, and_7_out, and_8_out, and_12_out, and_13_out,
       and_14_out, and_16_out, and_17_out, and_21_out, and_26_out, and_33_out, and_34_out, and_35_out,
       and_36_out, and_37_out, and_38_out, and_39_out, and_40_out, and_41_out, and_42_out, and_43_out,
       and_45_out, and_46_out, and_47_out, and_48_out, controlled_buffer_3_out, decoder_1_out2,
       decoder_1_out4, decoder_1_out5, decoder_1_out6, decoder_1_out7, decoder_2_out1, decoder_3_out0,
       decoder_3_out2, decoder_4_out0, decoder_4_out1, decoder_4_out2, decoder_4_out3, decoder_4_out4,
       decoder_4_out5, decoder_4_out6, n5_3_priority_encoder_1_q2, not_1_out, not_2_out, not_3_out,
       not_4_out, not_5_out, not_6_out, not_8_out, not_9_out, not_10_out, not_11_out, not_12_out, not_13_out,
       not_14_out, or_1_out, or_4_out, or_5_out, or_7_out, or_8_out, or_9_out, or_11_out;
  wire [1:0] controlled_buffer_7_out, controlled_buffer_8_out, controlled_buffer_9_out, n4_2_encoder_1_q0,
       or_12_out;
  wire [2:0] multiplexer_3_out, n5_3_priority_encoder_2_q0, undriven, undriven_2;
  wire [6:0] and_18_out;
  wire [7:0] and_27_out;
  wire [7:3] multiplexer_2_out;
  wire [15:0] demultiplexer_1_out0, demultiplexer_1_out1, demultiplexer_1_out2, demultiplexer_1_out3,
       demultiplexer_1_out4, demultiplexer_1_out5, demultiplexer_1_out6;

  not not_1 (not_1_out, and_3_out);
  and and_1 (and_1_out, A19, not_1_out, A18);
  or or_1 (or_1_out, A19, not_12_out);
  and and_2 (and_2_out, A17, not_13_out);
  and and_3 (and_3_out, or_1_out, multiplexer_2_out[5]);
  _4_2_encoder u_4_2_encoder_1 (
    .A2(and_2_out), .A1(and_3_out), .A0(or_4_out), .Q1(n4_2_encoder_1_q0[1]), .Q0(n4_2_encoder_1_q0[0]));  // open: A3
  Multiplexer #(.select(2), .width(3)) multiplexer_1 (
    .in0({ALU_instruction, 2'b00}), .in1(n5_3_priority_encoder_2_q0), .in2(undriven_2), .out(RAM_bus_cntl),
    .sel(n4_2_encoder_1_q0));  // open: in3
  or or_2 (RAM_rd, and_13_out, and_7_out, multiplexer_2_out[6], and_8_out);
  or or_3 (RAM_wrt, and_6_out, and_14_out);
  and and_4 (iprt_rd, not_2_out, or_5_out);
  and and_5 (and_5_out, not_11_out, and_18_out[6]);
  or or_4 (or_4_out, and_1_out, and_5_out);
  not not_2 (not_2_out, UIPRT_instruction);
  or or_5 (or_5_out, and_12_out, multiplexer_2_out[3]);
  or or_6 (iprt_sel, and_18_out[4], and_16_out, multiplexer_2_out[4]);
  and and_6 (and_6_out, decoder_3_out0, decoder_2_out1, A19);
  and and_7 (and_7_out, decoder_3_out0, not_4_out);
  and and_8 (and_8_out, A19, decoder_3_out0, ALU_instruction);
  and and_9 (reg_wrt__rec, and_17_out, not_5_out, not_6_out);
  and and_10 (reg_rd__rec, or_7_out, not_6_out);
  and and_11 (oprt_wrt__rec, and_21_out, not_6_out);
  and and_12 (and_12_out, and_18_out[3], not_6_out);
  and and_13 (and_13_out, and_18_out[6], not_6_out);
  and and_14 (and_14_out, and_26_out, not_6_out);
  and and_15 (n5_3_priority_encoder_2_q0[2], multiplexer_2_out[7], not_3_out);
  not not_3 (not_3_out, and_3_out);
  not not_4 (not_4_out, A19);
  not not_5 (not_5_out, A18);
  or or_7 (or_7_out, A18, and_18_out[0]);
  not not_6 (not_6_out, A19);
  Multiplexer #(.select(1), .width(8)) multiplexer_2 (
    .in0({and_27_out[7:6], and_27_out[6], A15, and_27_out[3:0]}),
    .in1({ALU_instruction, and_18_out[6], A18, and_18_out[4:3], register_address__rec, and_18_out[0]}),
    .out({multiplexer_2_out, register_address__send[0], register_address__send[1], reg_rd___send}), .sel(A19));
  and and_16 (and_16_out, UIPRT_instruction, A23);
  assign bus_out_cntl__rec[2] = A18 ? 1'b0 : 1'bz;  // Controlled_Buffer controlled_buffer_1
  assign bus_out_cntl__rec[2] = not_9_out ? n5_3_priority_encoder_1_q2 : 1'bz;  // Controlled_Buffer controlled_buffer_2
  and and_17 (and_17_out, decoder_3_out0, decoder_2_out1);
  and and_18 (and_18_out[0], decoder_3_out0, or_8_out);
  and and_19 (register_address__rec[0], A22, decoder_3_out0);
  and and_20 (register_address__rec[1], A23, decoder_3_out0);
  and and_21 (and_21_out, decoder_2_out1, oprt_is_rec);
  and and_22 (oprt_sel__rec, oprt_is_rec, A22);
  and and_23 (and_18_out[3], decoder_3_out2, or_9_out);
  and and_24 (and_18_out[4], decoder_3_out2, A23);
  and and_25 (and_18_out[6], A18, not_8_out);
  and and_26 (and_26_out, A18, decoder_2_out1);
  and and_27 (and_27_out[0], A13, not_12_out);
  and and_28 (and_27_out[1], A13, A15);
  and and_29 (and_27_out[2], A13, A14);
  and and_30 (and_27_out[3], not_12_out, not_14_out);
  and and_31 (and_27_out[6], decoder_1_out5, not_12_out);
  assign bus_out_cntl__send = ~undriven;  // NOT_Gate not_7, 3 bits wide
  Decoder #(.select(3), .tristate("false")) decoder_1 (
    .out2(decoder_1_out2), .out4(decoder_1_out4), .out5(decoder_1_out5), .out6(decoder_1_out6),
    .out7(decoder_1_out7), .sel(undriven));  // open: out0, out1, out3
  or or_8 (or_8_out, ALU_instruction, and_33_out, CP_instruction);
  or or_9 (or_9_out, decoder_2_out1, ALU_instruction);
  not not_8 (not_8_out, decoder_2_out1);
  not not_9 (not_9_out, A18);
  assign controlled_buffer_3_out = not_9_out ? ALU_instruction : 1'bz;  // Controlled_Buffer controlled_buffer_3
  _5_3_priority_encoder u_5_3_priority_encoder_1 (
    .A4(controlled_buffer_3_out), .A3(1'b0), .A2(A18), .A1(1'b0), .A0(1'b0), .Q2(n5_3_priority_encoder_1_q2),
    .Q1(bus_out_cntl__rec[1]), .Q0(bus_out_cntl__rec[0]));
  not not_10 (not_10_out, decoder_1_out5);
  and and_32 (decoder_1_out2, decoder_2_out1, or_11_out, not_13_out);
  assign decoder_1_out4 = not_10_out ? ALU_instruction : 1'bz;  // Controlled_Buffer controlled_buffer_4
  assign decoder_1_out6 = not_10_out ? and_17_out : 1'bz;  // Controlled_Buffer controlled_buffer_5
  assign decoder_1_out7 = not_10_out ? and_21_out : 1'bz;  // Controlled_Buffer controlled_buffer_6
  _5_3_priority_encoder u_5_3_priority_encoder_2 (
    .A4(1'b0), .A3(ALU_instruction), .A2(1'b0), .A1(and_17_out), .A0(and_21_out), .Q2(and_27_out[7]),
    .Q1(n5_3_priority_encoder_2_q0[1]), .Q0(n5_3_priority_encoder_2_q0[0]));
  and and_33 (and_33_out, decoder_2_out1, A19);
  or or_10 (decoder_1_out5, A12, and_34_out);
  and and_34 (and_34_out, A19, A18);
  or or_11 (or_11_out, A18, A17);
  Decoder #(.select(3), .tristate("false")) decoder_2 (
    .out0(ALU_instruction), .out1(decoder_2_out1), .out2(JP_instruction), .out3(CP_instruction),
    .out4(PON_POFF_instruction), .out5(PC_instruction), .out6(UIP_instruction), .out7(UIPRT_instruction),
    .sel({A31, A30, A29}));
  and and_35 (and_35_out, A17, A19);
  and and_36 (and_36_out, A17, not_11_out);
  Decoder #(.select(2), .tristate("false")) decoder_3 (
    .out0(decoder_3_out0), .out2(decoder_3_out2), .out3(oprt_is_rec), .sel({A21, A20}));  // open: out1
  assign controlled_buffer_7_out = JP_instruction ? 2'b00 : 2'bz;  // Controlled_Buffer controlled_buffer_7
  assign controlled_buffer_8_out = and_35_out ? 2'b01 : 2'bz;  // Controlled_Buffer controlled_buffer_8
  assign controlled_buffer_9_out = and_36_out ? 2'b10 : 2'bz;  // Controlled_Buffer controlled_buffer_9
  not not_11 (not_11_out, A19);
  Multiplexer #(.select(2), .width(3)) multiplexer_3 (
    .in0(3'b110), .in1(bus_out_cntl__rec), .in2(bus_out_cntl__send), .out(multiplexer_3_out), .sel(or_12_out));  // open: in3
  Decoder #(.select(3), .tristate("false")) decoder_4 (
    .out0(decoder_4_out0), .out1(decoder_4_out1), .out2(decoder_4_out2), .out3(decoder_4_out3),
    .out4(decoder_4_out4), .out5(decoder_4_out5), .out6(decoder_4_out6), .sel(multiplexer_3_out));  // open: out7
  assign or_12_out = controlled_buffer_7_out | controlled_buffer_8_out | controlled_buffer_9_out;  // OR_Gate or_12, 2 bits wide
  and and_37 (and_37_out, decoder_4_out0, A17);
  assign to_oprt_bus = and_37_out ? demultiplexer_1_out0 : 16'bz;  // Controlled_Buffer controlled_buffer_10
  not not_12 (not_12_out, A17);
  not not_13 (not_13_out, A16);
  and and_38 (and_38_out, decoder_4_out1, A17);
  assign to_Register_bus = and_38_out ? demultiplexer_1_out1 : 16'bz;  // Controlled_Buffer controlled_buffer_11
  not not_14 (not_14_out, A13);
  Demultiplexer #(.select(3), .width(16), .tristate("false")) demultiplexer_1 (
    .out0(demultiplexer_1_out0), .out1(demultiplexer_1_out1), .out2(demultiplexer_1_out2),
    .out3(demultiplexer_1_out3), .out4(demultiplexer_1_out4), .out5(demultiplexer_1_out5),
    .out6(demultiplexer_1_out6), .in({A15, A14, A13, A12, A11, A10, A9, A8, A7, A6, A5, A4, A3, A2, A1, A0}),
    .sel(multiplexer_3_out));  // open: out7
  and and_39 (and_39_out, decoder_4_out2, A17);
  assign to_RAM_adr__bus = and_39_out ? demultiplexer_1_out2 : 16'bz;  // Controlled_Buffer controlled_buffer_12
  and and_40 (and_40_out, decoder_4_out3, A17);
  and and_41 (and_41_out, decoder_4_out4, A17);
  assign to_ALU_B_bus = and_40_out ? demultiplexer_1_out3 : 16'bz;  // Controlled_Buffer controlled_buffer_13
  assign to_ALU_A_bus = and_41_out ? demultiplexer_1_out4 : 16'bz;  // Controlled_Buffer controlled_buffer_14
  and and_42 (and_42_out, decoder_4_out5, A17);
  assign to_RAM_data_bus = and_42_out ? demultiplexer_1_out5 : 16'bz;  // Controlled_Buffer controlled_buffer_15
  and and_43 (and_43_out, decoder_4_out6, A17);
  assign to_P_C__Control = and_43_out ? demultiplexer_1_out6 : 16'bz;  // Controlled_Buffer controlled_buffer_16
  and and_44 (Cndt_prime_l_Inst, not_12_out, A11);
  and and_45 (and_45_out, decoder_3_out0, A19);
  or or_13 (reg_is_send, and_45_out, and_46_out);
  and and_46 (and_46_out, not_12_out, A13);
  and and_47 (and_47_out, decoder_3_out2, A19);
  and and_48 (and_48_out, not_14_out, not_12_out);
  and and_49 (reg_is_rec, decoder_3_out0, not_11_out);
  and and_50 (iprt_is_rec, not_11_out, decoder_3_out2);
  or or_14 (iprt_is_send, and_47_out, and_48_out);

  assign ALU_cntl0 = A26;
  assign ALU_cntl1 = A27;
  assign ALU_cntl2 = A28;
  assign ALU_S_A = A25;
  assign Pin_Number = {A2, A1, A0};
  assign PON_POFF = A24;
  assign Test_S = A10;
  assign Test_S_2 = A9;
  assign Test_S_3 = A8;
  assign Test_S_4 = A7;
  assign Test_S_5 = A6;
  assign Test_S_6 = A5;

  // Notes on the sheet:
  //   4 to 2
  //   Receiving data medium decoder and controller
  //   Sending data medium decoder and controller
  //   5
  //   to
  //   3
  //   5
  //   to
  //   3
  //   Instruction Bits In
endmodule

module ALU (
  input  [15:0] B,
  input  [15:0] A,
  input  SUB_ADD,
  input  cntl2,
  input  cntl1,
  input  cntl0,
  input  CLK,
  input  ALU_op__sig__in,
  output [15:0] Q,
  output S,
  output C,
  output NZ,
  output Z
);

  wire and_1_out, and_2_out, and_4_out, and_5_out, and_6_out, and_7_out, and_8_out, and_9_out, and_10_out,
       and_11_out, and_12_out, and_13_out, and_14_out, and_15_out, and_16_out, and_17_out, and_18_out,
       and_19_out, and_20_out, decoder_1_out0, decoder_1_out1, decoder_1_out2, decoder_1_out3,
       decoder_1_out4, decoder_1_out5, decoder_1_out6, decoder_1_out7, full_adder_1_cout, full_adder_2_cout,
       full_adder_2_s, full_adder_3_cout, full_adder_3_s, full_adder_4_cout, full_adder_4_s,
       full_adder_5_cout, full_adder_5_s, full_adder_6_cout, full_adder_6_s, full_adder_7_cout,
       full_adder_7_s, full_adder_8_cout, full_adder_8_s, full_adder_9_cout, full_adder_9_s,
       full_adder_10_cout, full_adder_10_s, full_adder_11_cout, full_adder_11_s, full_adder_12_cout,
       full_adder_12_s, full_adder_13_cout, full_adder_13_s, full_adder_14_cout, full_adder_14_s,
       full_adder_15_cout, full_adder_15_s, full_adder_16_cout, full_adder_16_s, multiplexer_2_out,
       multiplexer_3_out, multiplexer_5_out, multiplexer_7_out, multiplexer_9_out, multiplexer_12_out,
       multiplexer_14_out, multiplexer_15_out, multiplexer_17_out, multiplexer_19_out, multiplexer_21_out,
       multiplexer_24_out, multiplexer_25_out, multiplexer_27_out, multiplexer_29_out, multiplexer_31_out,
       not_1_out, not_2_out, not_3_out, not_4_out, not_5_out, not_6_out, not_7_out, not_8_out, not_9_out,
       not_10_out, not_11_out, not_12_out, not_13_out, not_14_out, not_15_out, not_16_out, not_17_out,
       not_18_out, not_20_out, not_21_out, not_22_out, not_23_out, not_24_out, not_25_out, not_26_out,
       not_27_out, not_28_out, not_29_out, not_30_out, not_31_out, not_32_out, not_33_out, not_34_out,
       not_35_out, not_36_out, or_1_out, or_2_out, or_3_out, or_4_out, or_5_out, or_6_out, or_7_out,
       or_8_out, or_9_out, or_10_out, or_11_out, or_12_out, or_13_out, or_14_out, or_15_out, or_16_out,
       or_17_out, or_18_out, or_19_out, xor_1_out, xor_2_out, xor_3_out, xor_4_out, xor_5_out, xor_6_out,
       xor_7_out, xor_8_out, xor_9_out, xor_10_out, xor_11_out, xor_12_out, xor_13_out, xor_14_out,
       xor_15_out, xor_16_out;
  wire [3:0] and_3_out;

  not not_1 (not_1_out, 1'b1);
  or or_1 (or_1_out, B[15], A[15]);
  and and_1 (and_1_out, B[15], A[15]);
  xor xor_1 (xor_1_out, B[15], A[15]);
  Multiplexer #(.select(3), .width(1)) multiplexer_1 (
    .in0(A[14]), .in1(A[0]), .in2(A[14]), .in3(not_1_out), .in4(xor_1_out), .in5(or_1_out), .in6(and_1_out),
    .in7(and_3_out[3]), .out(Q[15]), .sel({cntl2, cntl1, cntl0}));
  not not_2 (not_2_out, Q[14]);
  not not_3 (not_3_out, Q[15]);
  not not_4 (not_4_out, B[15]);
  Multiplexer #(.select(1), .width(1)) multiplexer_2 (
    .in0(B[15]), .in1(not_4_out), .out(multiplexer_2_out), .sel(SUB_ADD));
  full_adder full_adder_1 (
    .Cout(full_adder_1_cout), .A(multiplexer_2_out), .B(A[15]), .S(and_3_out[3]), .Cin(full_adder_2_cout));
  not not_5 (not_5_out, Q[9]);
  not not_6 (not_6_out, Q[8]);
  not not_7 (not_7_out, Q[11]);
  not not_8 (not_8_out, Q[12]);
  not not_9 (not_9_out, Q[13]);
  not not_10 (not_10_out, Q[7]);
  not not_11 (not_11_out, Q[10]);
  and and_2 (and_2_out, not_3_out, not_2_out, not_9_out, not_8_out, not_7_out, not_11_out, not_5_out, not_6_out, not_10_out);
  and and_3 (and_3_out[0], and_2_out, and_4_out);
  or or_2 (or_2_out, B[14], A[14]);
  xor xor_2 (xor_2_out, B[14], A[14]);
  not not_12 (not_12_out, Q[6]);
  not not_13 (not_13_out, Q[4]);
  not not_14 (not_14_out, Q[5]);
  not not_15 (not_15_out, Q[2]);
  not not_16 (not_16_out, Q[1]);
  not not_17 (not_17_out, Q[0]);
  not not_18 (not_18_out, Q[3]);
  and and_4 (and_4_out, not_12_out, not_14_out, not_13_out, not_18_out, not_15_out, not_16_out, not_17_out);
  not not_19 (and_3_out[1], and_3_out[0]);
  not not_20 (not_20_out, B[14]);
  Multiplexer #(.select(1), .width(1)) multiplexer_3 (
    .in0(B[14]), .in1(not_20_out), .out(multiplexer_3_out), .sel(SUB_ADD));
  full_adder full_adder_2 (
    .Cout(full_adder_2_cout), .A(multiplexer_3_out), .B(A[14]), .S(full_adder_2_s), .Cin(full_adder_3_cout));
  and and_5 (and_5_out, B[14], A[14]);
  Multiplexer #(.select(3), .width(1)) multiplexer_4 (
    .in0(A[13]), .in1(A[15]), .in2(A[13]), .in3(A[15]), .in4(xor_2_out), .in5(or_2_out), .in6(and_5_out),
    .in7(full_adder_2_s), .out(Q[14]), .sel({cntl2, cntl1, cntl0}));
  xor xor_3 (xor_3_out, B[13], A[13]);
  not not_21 (not_21_out, B[13]);
  Multiplexer #(.select(1), .width(1)) multiplexer_5 (
    .in0(B[13]), .in1(not_21_out), .out(multiplexer_5_out), .sel(SUB_ADD));
  full_adder full_adder_3 (
    .Cout(full_adder_3_cout), .A(multiplexer_5_out), .B(A[13]), .S(full_adder_3_s), .Cin(full_adder_4_cout));
  or or_3 (or_3_out, B[13], A[13]);
  and and_6 (and_6_out, B[13], A[13]);
  Multiplexer #(.select(3), .width(1)) multiplexer_6 (
    .in0(A[12]), .in1(A[14]), .in2(A[12]), .in3(A[14]), .in4(xor_3_out), .in5(or_3_out), .in6(and_6_out),
    .in7(full_adder_3_s), .out(Q[13]), .sel({cntl2, cntl1, cntl0}));
  xor xor_4 (xor_4_out, B[12], A[12]);
  not not_22 (not_22_out, B[12]);
  Multiplexer #(.select(1), .width(1)) multiplexer_7 (
    .in0(B[12]), .in1(not_22_out), .out(multiplexer_7_out), .sel(SUB_ADD));
  and and_7 (and_7_out, B[12], A[12]);
  or or_4 (or_4_out, B[12], A[12]);
  Multiplexer #(.select(3), .width(1)) multiplexer_8 (
    .in0(A[11]), .in1(A[13]), .in2(A[11]), .in3(A[13]), .in4(xor_4_out), .in5(or_4_out), .in6(and_7_out),
    .in7(full_adder_4_s), .out(Q[12]), .sel({cntl2, cntl1, cntl0}));
  full_adder full_adder_4 (
    .Cout(full_adder_4_cout), .A(multiplexer_7_out), .B(A[12]), .S(full_adder_4_s), .Cin(full_adder_5_cout));
  Multiplexer #(.select(1), .width(1)) multiplexer_9 (
    .in0(B[11]), .in1(not_23_out), .out(multiplexer_9_out), .sel(SUB_ADD));
  xor xor_5 (xor_5_out, B[11], A[11]);
  and and_8 (and_8_out, B[11], A[11]);
  or or_5 (or_5_out, B[11], A[11]);
  Multiplexer #(.select(3), .width(1)) multiplexer_10 (
    .in0(A[10]), .in1(A[12]), .in2(A[10]), .in3(A[12]), .in4(xor_5_out), .in5(or_5_out), .in6(and_8_out),
    .in7(full_adder_5_s), .out(Q[11]), .sel({cntl2, cntl1, cntl0}));
  not not_23 (not_23_out, B[11]);
  full_adder full_adder_5 (
    .Cout(full_adder_5_cout), .A(multiplexer_9_out), .B(A[11]), .S(full_adder_5_s), .Cin(full_adder_6_cout));
  or or_6 (or_6_out, B[10], A[10]);
  and and_9 (and_9_out, B[10], A[10]);
  xor xor_6 (xor_6_out, B[10], A[10]);
  Multiplexer #(.select(3), .width(1)) multiplexer_11 (
    .in0(A[9]), .in1(A[11]), .in2(A[9]), .in3(A[11]), .in4(xor_6_out), .in5(or_6_out), .in6(and_9_out),
    .in7(full_adder_6_s), .out(Q[10]), .sel({cntl2, cntl1, cntl0}));
  not not_24 (not_24_out, B[10]);
  Multiplexer #(.select(1), .width(1)) multiplexer_12 (
    .in0(B[10]), .in1(not_24_out), .out(multiplexer_12_out), .sel(SUB_ADD));
  full_adder full_adder_6 (
    .Cout(full_adder_6_cout), .A(multiplexer_12_out), .B(A[10]), .S(full_adder_6_s), .Cin(full_adder_7_cout));
  or or_7 (or_7_out, B[9], A[9]);
  xor xor_7 (xor_7_out, B[9], A[9]);
  Multiplexer #(.select(3), .width(1)) multiplexer_13 (
    .in0(A[8]), .in1(A[10]), .in2(A[8]), .in3(A[10]), .in4(xor_7_out), .in5(or_7_out), .in6(and_10_out),
    .in7(full_adder_7_s), .out(Q[9]), .sel({cntl2, cntl1, cntl0}));
  not not_25 (not_25_out, B[9]);
  Multiplexer #(.select(1), .width(1)) multiplexer_14 (
    .in0(B[9]), .in1(not_25_out), .out(multiplexer_14_out), .sel(SUB_ADD));
  full_adder full_adder_7 (
    .Cout(full_adder_7_cout), .A(multiplexer_14_out), .B(A[9]), .S(full_adder_7_s), .Cin(full_adder_8_cout));
  and and_10 (and_10_out, B[9], A[9]);
  xor xor_8 (xor_8_out, B[8], A[8]);
  or or_8 (or_8_out, B[8], A[8]);
  not not_26 (not_26_out, B[8]);
  Multiplexer #(.select(1), .width(1)) multiplexer_15 (
    .in0(B[8]), .in1(not_26_out), .out(multiplexer_15_out), .sel(SUB_ADD));
  full_adder full_adder_8 (
    .Cout(full_adder_8_cout), .A(multiplexer_15_out), .B(A[8]), .S(full_adder_8_s), .Cin(full_adder_9_cout));
  and and_11 (and_11_out, B[8], A[8]);
  Multiplexer #(.select(3), .width(1)) multiplexer_16 (
    .in0(A[7]), .in1(A[9]), .in2(A[7]), .in3(A[9]), .in4(xor_8_out), .in5(or_8_out), .in6(and_11_out),
    .in7(full_adder_8_s), .out(Q[8]), .sel({cntl2, cntl1, cntl0}));
  or or_9 (or_9_out, B[7], A[7]);
  xor xor_9 (xor_9_out, B[7], A[7]);
  not not_27 (not_27_out, B[7]);
  Multiplexer #(.select(1), .width(1)) multiplexer_17 (
    .in0(B[7]), .in1(not_27_out), .out(multiplexer_17_out), .sel(SUB_ADD));
  full_adder full_adder_9 (
    .Cout(full_adder_9_cout), .A(multiplexer_17_out), .B(A[7]), .S(full_adder_9_s), .Cin(full_adder_10_cout));
  and and_12 (and_12_out, B[7], A[7]);
  Multiplexer #(.select(3), .width(1)) multiplexer_18 (
    .in0(A[6]), .in1(A[8]), .in2(A[6]), .in3(A[8]), .in4(xor_9_out), .in5(or_9_out), .in6(and_12_out),
    .in7(full_adder_9_s), .out(Q[7]), .sel({cntl2, cntl1, cntl0}));
  xor xor_10 (xor_10_out, B[6], A[6]);
  not not_28 (not_28_out, B[6]);
  Multiplexer #(.select(1), .width(1)) multiplexer_19 (
    .in0(B[6]), .in1(not_28_out), .out(multiplexer_19_out), .sel(SUB_ADD));
  full_adder full_adder_10 (
    .Cout(full_adder_10_cout), .A(multiplexer_19_out), .B(A[6]), .S(full_adder_10_s), .Cin(full_adder_11_cout));
  and and_13 (and_13_out, B[6], A[6]);
  or or_10 (or_10_out, B[6], A[6]);
  Multiplexer #(.select(3), .width(1)) multiplexer_20 (
    .in0(A[5]), .in1(A[7]), .in2(A[5]), .in3(A[7]), .in4(xor_10_out), .in5(or_10_out), .in6(and_13_out),
    .in7(full_adder_10_s), .out(Q[6]), .sel({cntl2, cntl1, cntl0}));
  Multiplexer #(.select(1), .width(1)) multiplexer_21 (
    .in0(B[5]), .in1(not_29_out), .out(multiplexer_21_out), .sel(SUB_ADD));
  xor xor_11 (xor_11_out, B[5], A[5]);
  and and_14 (and_14_out, B[5], A[5]);
  or or_11 (or_11_out, B[5], A[5]);
  Multiplexer #(.select(3), .width(1)) multiplexer_22 (
    .in0(A[4]), .in1(A[6]), .in2(A[4]), .in3(A[6]), .in4(xor_11_out), .in5(or_11_out), .in6(and_14_out),
    .in7(full_adder_11_s), .out(Q[5]), .sel({cntl2, cntl1, cntl0}));
  not not_29 (not_29_out, B[5]);
  full_adder full_adder_11 (
    .Cout(full_adder_11_cout), .A(multiplexer_21_out), .B(A[5]), .S(full_adder_11_s), .Cin(full_adder_12_cout));
  or or_12 (or_12_out, B[4], A[4]);
  xor xor_12 (xor_12_out, B[4], A[4]);
  Multiplexer #(.select(3), .width(1)) multiplexer_23 (
    .in0(A[3]), .in1(A[5]), .in2(A[3]), .in3(A[5]), .in4(xor_12_out), .in5(or_12_out), .in6(and_15_out),
    .in7(full_adder_12_s), .out(Q[4]), .sel({cntl2, cntl1, cntl0}));
  not not_30 (not_30_out, B[4]);
  Multiplexer #(.select(1), .width(1)) multiplexer_24 (
    .in0(B[4]), .in1(not_30_out), .out(multiplexer_24_out), .sel(SUB_ADD));
  full_adder full_adder_12 (
    .Cout(full_adder_12_cout), .A(multiplexer_24_out), .B(A[4]), .S(full_adder_12_s), .Cin(full_adder_13_cout));
  and and_15 (and_15_out, B[4], A[4]);
  xor xor_13 (xor_13_out, B[3], A[3]);
  or or_13 (or_13_out, B[3], A[3]);
  _3_1_MUX u_3_1_mux_1 (
    .cntl0(or_18_out), .cnt1(or_17_out), .cntl2(or_19_out), .A2(A[0]), .A1(A[15]), .A0(full_adder_1_cout),
    .Q(and_3_out[2]));
  not not_31 (not_31_out, B[3]);
  Multiplexer #(.select(1), .width(1)) multiplexer_25 (
    .in0(B[3]), .in1(not_31_out), .out(multiplexer_25_out), .sel(SUB_ADD));
  full_adder full_adder_13 (
    .Cout(full_adder_13_cout), .A(multiplexer_25_out), .B(A[3]), .S(full_adder_13_s), .Cin(full_adder_14_cout));
  and and_16 (and_16_out, B[3], A[3]);
  Multiplexer #(.select(3), .width(1)) multiplexer_26 (
    .in0(A[2]), .in1(A[4]), .in2(A[2]), .in3(A[4]), .in4(xor_13_out), .in5(or_13_out), .in6(and_16_out),
    .in7(full_adder_13_s), .out(Q[3]), .sel({cntl2, cntl1, cntl0}));
  xor xor_14 (xor_14_out, B[2], A[2]);
  or or_14 (or_14_out, B[2], A[2]);
  not not_32 (not_32_out, B[2]);
  Multiplexer #(.select(1), .width(1)) multiplexer_27 (
    .in0(B[2]), .in1(not_32_out), .out(multiplexer_27_out), .sel(SUB_ADD));
  full_adder full_adder_14 (
    .Cout(full_adder_14_cout), .A(multiplexer_27_out), .B(A[2]), .S(full_adder_14_s), .Cin(full_adder_15_cout));
  and and_17 (and_17_out, B[2], A[2]);
  Multiplexer #(.select(3), .width(1)) multiplexer_28 (
    .in0(A[1]), .in1(A[3]), .in2(A[1]), .in3(A[3]), .in4(xor_14_out), .in5(or_14_out), .in6(and_17_out),
    .in7(full_adder_14_s), .out(Q[2]), .sel({cntl2, cntl1, cntl0}));
  xor xor_15 (xor_15_out, B[1], A[1]);
  Register #(.width(4)) register_1 (.D(and_3_out), .Q({S, C, NZ, Z}), .clk(and_20_out));  // open: en, clr
  not not_33 (not_33_out, B[1]);
  Multiplexer #(.select(1), .width(1)) multiplexer_29 (
    .in0(B[1]), .in1(not_33_out), .out(multiplexer_29_out), .sel(SUB_ADD));
  full_adder full_adder_15 (
    .Cout(full_adder_15_cout), .A(multiplexer_29_out), .B(A[1]), .S(full_adder_15_s), .Cin(full_adder_16_cout));
  or or_15 (or_15_out, B[1], A[1]);
  and and_18 (and_18_out, B[1], A[1]);
  Multiplexer #(.select(3), .width(1)) multiplexer_30 (
    .in0(A[0]), .in1(A[2]), .in2(A[0]), .in3(A[2]), .in4(xor_15_out), .in5(or_15_out), .in6(and_18_out),
    .in7(full_adder_15_s), .out(Q[1]), .sel({cntl2, cntl1, cntl0}));
  not not_34 (not_34_out, 1'b1);
  xor xor_16 (xor_16_out, B[0], A[0]);
  not not_35 (not_35_out, B[0]);
  Multiplexer #(.select(1), .width(1)) multiplexer_31 (
    .in0(B[0]), .in1(not_35_out), .out(multiplexer_31_out), .sel(SUB_ADD));
  full_adder full_adder_16 (
    .Cout(full_adder_16_cout), .A(multiplexer_31_out), .B(A[0]), .S(full_adder_16_s), .Cin(SUB_ADD));
  and and_19 (and_19_out, B[0], A[0]);
  or or_16 (or_16_out, B[0], A[0]);
  Multiplexer #(.select(3), .width(1)) multiplexer_32 (
    .in0(A[15]), .in1(A[1]), .in2(not_34_out), .in3(A[1]), .in4(xor_16_out), .in5(or_16_out),
    .in6(and_19_out), .in7(full_adder_16_s), .out(Q[0]), .sel({cntl2, cntl1, cntl0}));
  Decoder #(.select(3), .tristate("false")) decoder_1 (
    .out0(decoder_1_out0), .out1(decoder_1_out1), .out2(decoder_1_out2), .out3(decoder_1_out3),
    .out4(decoder_1_out4), .out5(decoder_1_out5), .out6(decoder_1_out6), .out7(decoder_1_out7),
    .sel({cntl2, cntl1, cntl0}));
  or or_17 (or_17_out, decoder_1_out0, decoder_1_out2);
  or or_18 (or_18_out, decoder_1_out4, decoder_1_out5, decoder_1_out6, decoder_1_out7);
  or or_19 (or_19_out, decoder_1_out1, decoder_1_out3);
  not not_36 (not_36_out, CLK);
  and and_20 (and_20_out, not_36_out, ALU_op__sig__in);

  // Notes on the sheet:
  //   OZ-2 ALU
  //   Copyright Ben Oztalay 2009
  //   +
  //   +
  //   +
  //   +
  //   +
  //   +
  //   +
  //   +
  //   +
  //   +
  //   +
  //   +
  //   3-1
  //   +
  //   +
  //   +
  //   +
endmodule

module Register_File (
  input  [15:0] Register_Data_Bus_in,
  input  ALU_instruction_signifier_in,
  input  CLK,
  input  Condition_Block_in,
  input  Read__rec,
  input  Write__rec,
  input  [1:0] Address__rec,
  input  [2:0] Bus_out_cntl__rec,
  input  Read__send,
  input  [1:0] Address__send,
  input  [2:0] Bus_out_cntl__send,
  input  Register_is_rec__sig,
  input  Register_is_send_sig,
  output [15:0] to_oprt_bus,
  output [15:0] to_Register_bus,
  output [15:0] to_RAM_adr__bus,
  output [15:0] to_ALU_B_bus,
  output [15:0] to_ALU_A_bus,
  output [15:0] to_oprt_bus_2,
  output [15:0] to_Register_bus_2,
  output [15:0] to_RAM_adr__bus_2,
  output [15:0] to_ALU_B_bus_2,
  output [15:0] to_ALU_A_bus_2,
  output [15:0] to_RAM_data_bus
);

  wire and_1_out, and_2_out, and_3_out, and_4_out, and_5_out, and_6_out, and_7_out, and_8_out, and_9_out,
       and_10_out, and_11_out, and_12_out, and_13_out, and_14_out, and_15_out, and_16_out, and_17_out,
       and_18_out, and_19_out, decoder_1_out0, decoder_1_out1, decoder_1_out2, decoder_1_out3,
       decoder_1_out4, decoder_2_out0, decoder_2_out1, decoder_2_out2, decoder_2_out3, decoder_2_out4,
       decoder_2_out5, decoder_3_out0, decoder_3_out1, decoder_3_out2, decoder_3_out3, not_1_out, not_2_out,
       or_1_out;
  wire [15:0] controlled_buffer_4_out, demultiplexer_1_out0, demultiplexer_1_out1, demultiplexer_1_out2,
       demultiplexer_1_out3, demultiplexer_1_out4, demultiplexer_2_out0, demultiplexer_2_out1,
       demultiplexer_2_out2, demultiplexer_2_out3, demultiplexer_3_out0, demultiplexer_3_out1,
       demultiplexer_3_out2, demultiplexer_3_out3, demultiplexer_3_out4, demultiplexer_3_out5,
       multiplexer_1_out, multiplexer_2_out, register_1_q, register_2_q, register_3_q, register_4_q;

  Decoder #(.select(3), .tristate("false")) decoder_1 (
    .out0(decoder_1_out0), .out1(decoder_1_out1), .out2(decoder_1_out2), .out3(decoder_1_out3),
    .out4(decoder_1_out4), .sel(Bus_out_cntl__rec));  // open: out5, out6, out7
  and and_1 (and_1_out, decoder_1_out0, Condition_Block_in, and_14_out);
  assign to_oprt_bus = and_1_out ? demultiplexer_1_out0 : 16'bz;  // Controlled_Buffer controlled_buffer_1
  and and_2 (and_2_out, decoder_1_out1, Condition_Block_in, and_14_out);
  assign to_Register_bus = and_2_out ? demultiplexer_1_out1 : 16'bz;  // Controlled_Buffer controlled_buffer_2
  Multiplexer #(.select(2), .width(16)) multiplexer_1 (
    .in0(register_1_q), .in1(register_2_q), .in2(register_3_q), .in3(register_4_q), .out(multiplexer_1_out),
    .sel(Address__rec));
  Demultiplexer #(.select(3), .width(16), .tristate("false")) demultiplexer_1 (
    .out0(demultiplexer_1_out0), .out1(demultiplexer_1_out1), .out2(demultiplexer_1_out2),
    .out3(demultiplexer_1_out3), .out4(demultiplexer_1_out4), .in(multiplexer_1_out), .sel(Bus_out_cntl__rec));  // open: out5, out6, out7
  and and_3 (and_3_out, decoder_1_out2, Condition_Block_in, and_14_out);
  assign to_RAM_adr__bus = and_3_out ? demultiplexer_1_out2 : 16'bz;  // Controlled_Buffer controlled_buffer_3
  assign controlled_buffer_4_out = ALU_instruction_signifier_in ? Register_Data_Bus_in : 16'bz;  // Controlled_Buffer controlled_buffer_4
  assign controlled_buffer_4_out = not_1_out ? demultiplexer_2_out0 : 16'bz;  // Controlled_Buffer controlled_buffer_5
  Register #(.width(16)) register_1 (.D(controlled_buffer_4_out), .Q(register_1_q), .clk(or_1_out));  // open: en, clr
  or or_1 (or_1_out, and_4_out, and_5_out);
  and and_4 (and_4_out, not_2_out, ALU_instruction_signifier_in);
  and and_5 (and_5_out, decoder_3_out0, not_2_out, Condition_Block_in, and_15_out);
  and and_6 (and_6_out, decoder_1_out3, Condition_Block_in, and_14_out);
  Demultiplexer #(.select(2), .width(16), .tristate("false")) demultiplexer_2 (
    .out0(demultiplexer_2_out0), .out1(demultiplexer_2_out1), .out2(demultiplexer_2_out2),
    .out3(demultiplexer_2_out3), .in(Register_Data_Bus_in), .sel(Address__rec));
  Register #(.width(16)) register_2 (.D(demultiplexer_2_out1), .Q(register_2_q), .clk(and_7_out));  // open: en, clr
  and and_7 (and_7_out, decoder_3_out1, not_2_out, Condition_Block_in, and_15_out);
  and and_8 (and_8_out, decoder_1_out4, Condition_Block_in, and_14_out);
  assign to_ALU_B_bus = and_6_out ? demultiplexer_1_out3 : 16'bz;  // Controlled_Buffer controlled_buffer_6
  Register #(.width(16)) register_3 (.D(demultiplexer_2_out2), .Q(register_3_q), .clk(and_9_out));  // open: en, clr
  and and_9 (and_9_out, decoder_3_out2, not_2_out, Condition_Block_in, and_15_out);
  assign to_ALU_A_bus = and_8_out ? demultiplexer_1_out4 : 16'bz;  // Controlled_Buffer controlled_buffer_7
  Register #(.width(16)) register_4 (.D(demultiplexer_2_out3), .Q(register_4_q), .clk(and_10_out));  // open: en, clr
  and and_10 (and_10_out, decoder_3_out3, not_2_out, Condition_Block_in, and_15_out);
  Decoder #(.select(3), .tristate("false")) decoder_2 (
    .out0(decoder_2_out0), .out1(decoder_2_out1), .out2(decoder_2_out2), .out3(decoder_2_out3),
    .out4(decoder_2_out4), .out5(decoder_2_out5), .sel(Bus_out_cntl__send));  // open: out6, out7
  and and_11 (and_11_out, decoder_2_out0, Condition_Block_in, and_16_out);
  assign to_oprt_bus_2 = and_11_out ? demultiplexer_3_out0 : 16'bz;  // Controlled_Buffer controlled_buffer_8
  and and_12 (and_12_out, decoder_2_out1, Condition_Block_in, and_16_out);
  assign to_Register_bus_2 = and_12_out ? demultiplexer_3_out1 : 16'bz;  // Controlled_Buffer controlled_buffer_9
  not not_1 (not_1_out, ALU_instruction_signifier_in);
  not not_2 (not_2_out, CLK);
  Decoder #(.select(2), .tristate("false")) decoder_3 (
    .out0(decoder_3_out0), .out1(decoder_3_out1), .out2(decoder_3_out2), .out3(decoder_3_out3),
    .sel(Address__rec));
  Multiplexer #(.select(2), .width(16)) multiplexer_2 (
    .in0(register_1_q), .in1(register_2_q), .in2(register_3_q), .in3(register_4_q), .out(multiplexer_2_out),
    .sel(Address__send));
  Demultiplexer #(.select(3), .width(16), .tristate("false")) demultiplexer_3 (
    .out0(demultiplexer_3_out0), .out1(demultiplexer_3_out1), .out2(demultiplexer_3_out2),
    .out3(demultiplexer_3_out3), .out4(demultiplexer_3_out4), .out5(demultiplexer_3_out5),
    .in(multiplexer_2_out), .sel(Bus_out_cntl__send));  // open: out6, out7
  and and_13 (and_13_out, decoder_2_out2, Condition_Block_in, and_16_out);
  assign to_RAM_adr__bus_2 = and_13_out ? demultiplexer_3_out2 : 16'bz;  // Controlled_Buffer controlled_buffer_10
  and and_14 (and_14_out, Read__rec, Register_is_rec__sig);
  and and_15 (and_15_out, Write__rec, Register_is_rec__sig);
  and and_16 (and_16_out, Read__send, Register_is_send_sig);
  and and_17 (and_17_out, decoder_2_out3, Condition_Block_in, and_16_out);
  assign to_ALU_B_bus_2 = and_17_out ? demultiplexer_3_out3 : 16'bz;  // Controlled_Buffer controlled_buffer_11
  and and_18 (and_18_out, decoder_2_out4, Condition_Block_in, and_16_out);
  and and_19 (and_19_out, decoder_2_out5, Condition_Block_in, and_16_out);
  assign to_ALU_A_bus_2 = and_18_out ? demultiplexer_3_out4 : 16'bz;  // Controlled_Buffer controlled_buffer_12
  assign to_RAM_data_bus = and_19_out ? demultiplexer_3_out5 : 16'bz;  // Controlled_Buffer controlled_buffer_13
endmodule

module RAM (
  input  [15:0] RAM_Address_bus_in,
  input  [15:0] RAM_Data_bus_in,
  input  CLK,
  input  Condition_Block_in,
  input  Read,
  input  Write,
  input  [2:0] bus_out_cntl,
  output [15:0] to_oprt_bus,
  output [15:0] to_Register_bus,
  output [15:0] to_ALU_B_bus,
  output [15:0] to_ALU_A_bus
);

  wire and_1_out, and_2_out, and_3_out, and_4_out, and_5_out, and_6_out, and_7_out, decoder_1_out0,
       decoder_1_out1, decoder_1_out3, decoder_1_out4, not_1_out, not_2_out, not_3_out;
  wire [15:0] controlled_buffer_4_out, demultiplexer_1_out0, demultiplexer_1_out1, demultiplexer_1_out3,
       demultiplexer_1_out4, ram_1_data;

  Decoder #(.select(3), .tristate("false")) decoder_1 (
    .out0(decoder_1_out0), .out1(decoder_1_out1), .out3(decoder_1_out3), .out4(decoder_1_out4),
    .sel(bus_out_cntl));  // open: out2, out5, out6, out7
  and and_1 (and_1_out, decoder_1_out0, Read, Condition_Block_in);
  assign to_oprt_bus = and_1_out ? demultiplexer_1_out0 : 16'bz;  // Controlled_Buffer controlled_buffer_1
  RAM_part #(.addrWidth(16), .dataWidth(16)) ram_1 (
    .addr(RAM_Address_bus_in), .data(ram_1_data), .clk(and_2_out), .ld(Read));  // open: sel, clr
  and and_2 (and_2_out, Condition_Block_in, not_3_out, Write);
  and and_3 (and_3_out, decoder_1_out1, Read, Condition_Block_in);
  assign to_Register_bus = and_3_out ? demultiplexer_1_out1 : 16'bz;  // Controlled_Buffer controlled_buffer_2
  and and_4 (and_4_out, Write, not_1_out);
  assign ram_1_data = and_4_out ? RAM_Data_bus_in : 16'bz;  // Controlled_Buffer controlled_buffer_3
  not not_1 (not_1_out, Read);
  and and_5 (and_5_out, Read, not_2_out);
  assign controlled_buffer_4_out = and_5_out ? ram_1_data : 16'bz;  // Controlled_Buffer controlled_buffer_4
  not not_2 (not_2_out, Write);
  Demultiplexer #(.select(3), .width(16), .tristate("false")) demultiplexer_1 (
    .out0(demultiplexer_1_out0), .out1(demultiplexer_1_out1), .out3(demultiplexer_1_out3),
    .out4(demultiplexer_1_out4), .in(controlled_buffer_4_out), .sel(bus_out_cntl));  // open: out2, out5, out6, out7
  not not_3 (not_3_out, CLK);
  and and_6 (and_6_out, decoder_1_out3, Read, Condition_Block_in);
  assign to_ALU_B_bus = and_6_out ? demultiplexer_1_out3 : 16'bz;  // Controlled_Buffer controlled_buffer_5
  and and_7 (and_7_out, decoder_1_out4, Read, Condition_Block_in);
  assign to_ALU_A_bus = and_7_out ? demultiplexer_1_out4 : 16'bz;  // Controlled_Buffer controlled_buffer_6
endmodule

module Input_Port_Controller (
  input  P1_15,
  input  P1_14,
  input  P1_13,
  input  P1_12,
  input  P1_11,
  input  P1_10,
  input  P1_9,
  input  P1_8,
  input  P1_7,
  input  P1_6,
  input  P1_5,
  input  P1_4,
  input  P1_3,
  input  P1_2,
  input  P1_1,
  input  P1_0,
  input  P2_15,
  input  P2_14,
  input  P2_13,
  input  P2_12,
  input  P2_11,
  input  P2_10,
  input  P2_9,
  input  P2_8,
  input  P2_7,
  input  P2_6,
  input  P2_5,
  input  P2_4,
  input  P2_3,
  input  P2_2,
  input  P2_1,
  input  P2_0,
  input  CLK,
  input  Condition_Block_in,
  input  Read,
  input  Update,
  input  Port_Select,
  input  [2:0] bus_cntl__rec,
  input  [2:0] bus_cntl__send,
  input  iprt_is_rec,
  input  iprt_is_send,
  output [15:0] to_oprt_bus,
  output [15:0] to_Register_bus,
  output [15:0] to_RAM_adr__bus,
  output [15:0] to_ALU_B_bus,
  output [15:0] to_ALU_A_bus,
  output [15:0] to_RAM_data_bus
);

  wire and_1_out, and_2_out, and_3_out, and_4_out, and_5_out, and_6_out, and_7_out, and_8_out, and_9_out,
       decoder_1_out0, decoder_1_out1, decoder_1_out2, decoder_1_out3, decoder_1_out4, decoder_1_out5,
       not_1_out, not_2_out, not_3_out;
  wire [2:0] multiplexer_2_out;
  wire [15:0] demultiplexer_1_out0, demultiplexer_1_out1, demultiplexer_1_out2, demultiplexer_1_out3,
       demultiplexer_1_out4, demultiplexer_1_out5, multiplexer_1_out, register_1_q, register_2_q;

  and and_1 (and_1_out, not_1_out, Condition_Block_in, not_2_out, Update);
  not not_1 (not_1_out, Port_Select);
  Register #(.width(16)) register_1 (
    .D({P1_15, P1_14, P1_13, P1_12, P1_11, P1_10, P1_9, P1_8, P1_7, P1_6, P1_5, P1_4, P1_3, P1_2, P1_1, P1_0}),
    .Q(register_1_q), .clk(and_1_out));  // open: en, clr
  Decoder #(.select(3), .tristate("false")) decoder_1 (
    .out0(decoder_1_out0), .out1(decoder_1_out1), .out2(decoder_1_out2), .out3(decoder_1_out3),
    .out4(decoder_1_out4), .out5(decoder_1_out5), .sel(multiplexer_2_out));  // open: out6, out7
  and and_2 (and_2_out, decoder_1_out0, Condition_Block_in, Read);
  assign to_oprt_bus = and_2_out ? demultiplexer_1_out0 : 16'bz;  // Controlled_Buffer controlled_buffer_1
  and and_3 (and_3_out, decoder_1_out1, Condition_Block_in, Read);
  assign to_Register_bus = and_3_out ? demultiplexer_1_out1 : 16'bz;  // Controlled_Buffer controlled_buffer_2
  Multiplexer #(.select(1), .width(16)) multiplexer_1 (
    .in0(register_1_q), .in1(register_2_q), .out(multiplexer_1_out), .sel(Port_Select));
  Demultiplexer #(.select(3), .width(16), .tristate("false")) demultiplexer_1 (
    .out0(demultiplexer_1_out0), .out1(demultiplexer_1_out1), .out2(demultiplexer_1_out2),
    .out3(demultiplexer_1_out3), .out4(demultiplexer_1_out4), .out5(demultiplexer_1_out5),
    .in(multiplexer_1_out), .sel(multiplexer_2_out));  // open: out6, out7
  and and_4 (and_4_out, decoder_1_out2, Condition_Block_in, Read);
  assign to_RAM_adr__bus = and_4_out ? demultiplexer_1_out2 : 16'bz;  // Controlled_Buffer controlled_buffer_3
  and and_5 (and_5_out, decoder_1_out3, Condition_Block_in, Read);
  assign to_ALU_B_bus = and_5_out ? demultiplexer_1_out3 : 16'bz;  // Controlled_Buffer controlled_buffer_4
  and and_6 (and_6_out, decoder_1_out4, Condition_Block_in, Read);
  assign to_ALU_A_bus = and_6_out ? demultiplexer_1_out4 : 16'bz;  // Controlled_Buffer controlled_buffer_5
  Register #(.width(16)) register_2 (
    .D({P2_15, P2_14, P2_13, P2_12, P2_11, P2_10, P2_9, P2_8, P2_7, P2_6, P2_5, P2_4, P2_3, P2_2, P2_1, P2_0}),
    .Q(register_2_q), .clk(and_7_out));  // open: en, clr
  and and_7 (and_7_out, Update, not_2_out, Condition_Block_in, Port_Select);
  and and_8 (and_8_out, decoder_1_out5, Condition_Block_in, Read);
  assign to_RAM_data_bus = and_8_out ? demultiplexer_1_out5 : 16'bz;  // Controlled_Buffer controlled_buffer_6
  not not_2 (not_2_out, CLK);
  Multiplexer #(.select(1), .width(3)) multiplexer_2 (
    .in0(bus_cntl__rec), .in1(bus_cntl__send), .out(multiplexer_2_out), .sel(and_9_out));
  and and_9 (and_9_out, iprt_is_send, not_3_out);
  not not_3 (not_3_out, iprt_is_rec);
endmodule

module Input_Pin_Controller (
  input  A0,
  input  A1,
  input  A2,
  input  A3,
  input  A4,
  input  A5,
  input  A6,
  input  A7,
  input  [2:0] Pin_Number,
  input  CLK,
  input  Condition_Block_in,
  input  Check_Pin,
  input  Update_Pins,
  output N,
  output F
);

  wire and_1_out, and_2_out, not_1_out;
  wire [1:0] not_2_out;
  wire [7:0] register_1_q;

  not not_1 (not_1_out, CLK);
  Register #(.width(8)) register_1 (
    .D({A0, A1, A2, A3, A4, A5, A6, A7}), .Q(register_1_q), .clk(and_1_out));  // open: en, clr
  and and_1 (and_1_out, not_1_out, Condition_Block_in, Update_Pins);
  Multiplexer #(.select(3), .width(1)) multiplexer_1 (
    .in0(register_1_q[7]), .in1(register_1_q[6]), .in2(register_1_q[5]), .in3(register_1_q[4]),
    .in4(register_1_q[3]), .in5(register_1_q[2]), .in6(register_1_q[1]), .in7(register_1_q[0]),
    .out(not_2_out[1]), .sel(Pin_Number));
  and and_2 (and_2_out, not_1_out, Condition_Block_in, Check_Pin);
  not not_2 (not_2_out[0], not_2_out[1]);
  Register #(.width(2)) register_2 (.D(not_2_out), .Q({N, F}), .clk(and_2_out));  // open: en, clr
endmodule

module Condition_Block (
  input  Testing,
  input  Test_S,
  input  Test_C,
  input  Test_NZ,
  input  Test_Z,
  input  Test_N,
  input  Test_F,
  input  S,
  input  C,
  input  NZ,
  input  Z,
  input  N,
  input  F,
  output True
);

  wire and_1_out, and_2_out, and_3_out, and_4_out, and_5_out, and_6_out, not_1_out, or_1_out;

  not not_1 (not_1_out, Testing);
  and and_1 (and_1_out, Testing, Test_S, S);
  and and_2 (and_2_out, Testing, Test_C, C);
  and and_3 (and_3_out, Testing, Test_NZ, NZ);
  and and_4 (and_4_out, Testing, Test_Z, Z);
  and and_5 (and_5_out, Testing, Test_N, N);
  and and_6 (and_6_out, Testing, Test_F, F);
  or or_1 (or_1_out, and_1_out, and_2_out, and_3_out, and_4_out, and_5_out, and_6_out);
  or or_2 (True, or_1_out, not_1_out);
endmodule

module Output_Port_Controller (
  input  [15:0] Output_Port_Data_Bus,
  input  CLK,
  input  Condition_Block,
  input  Write,
  input  Port_Select,
  output OP1_15,
  output OP1_14,
  output OP1_13,
  output OP1_12,
  output OP1_11,
  output OP1_10,
  output OP1_9,
  output OP1_8,
  output OP1_7,
  output OP1_6,
  output OP1_5,
  output OP1_4,
  output OP1_3,
  output OP1_2,
  output OP1_1,
  output OP1_0,
  output OP2_15,
  output OP2_14,
  output OP2_13,
  output OP2_12,
  output OP2_11,
  output OP2_10,
  output OP2_9,
  output OP2_8,
  output OP2_7,
  output OP2_6,
  output OP2_5,
  output OP2_4,
  output OP2_3,
  output OP2_2,
  output OP2_1,
  output OP2_0
);

  wire and_1_out, and_2_out, not_1_out, not_2_out;

  Register #(.width(16)) register_1 (
    .D(Output_Port_Data_Bus),
    .Q({OP1_15, OP1_14, OP1_13, OP1_12, OP1_11, OP1_10, OP1_9, OP1_8, OP1_7, OP1_6, OP1_5, OP1_4, OP1_3, OP1_2, OP1_1, OP1_0}),
    .clk(and_1_out));  // open: en, clr
  and and_1 (and_1_out, not_2_out, Condition_Block, Write, not_1_out);
  not not_1 (not_1_out, Port_Select);
  Register #(.width(16)) register_2 (
    .D(Output_Port_Data_Bus),
    .Q({OP2_15, OP2_14, OP2_13, OP2_12, OP2_11, OP2_10, OP2_9, OP2_8, OP2_7, OP2_6, OP2_5, OP2_4, OP2_3, OP2_2, OP2_1, OP2_0}),
    .clk(and_2_out));  // open: en, clr
  and and_2 (and_2_out, not_2_out, Condition_Block, Write);
  not not_2 (not_2_out, CLK);
endmodule

module Output_Pin_Controller (
  input  [2:0] Pin_Number,
  input  CLK,
  input  Condition_Block,
  input  Write,
  input  Pin_on_off_selection,
  output OPN7,
  output OPN6,
  output OPN5,
  output OPN4,
  output OPN3,
  output OPN2,
  output OPN1,
  output OPN0
);

  wire and_1_out, and_2_out, and_3_out, and_4_out, and_5_out, and_6_out, and_7_out, and_8_out,
       decoder_1_out0, decoder_1_out1, decoder_1_out2, decoder_1_out3, decoder_1_out4, decoder_1_out5,
       decoder_1_out6, decoder_1_out7, demultiplexer_1_out0, demultiplexer_1_out1, demultiplexer_1_out2,
       demultiplexer_1_out3, demultiplexer_1_out4, demultiplexer_1_out5, demultiplexer_1_out6,
       demultiplexer_1_out7, not_1_out;

  and and_1 (and_1_out, Write, Condition_Block, decoder_1_out0, demultiplexer_1_out0);
  and and_2 (and_2_out, Write, Condition_Block, decoder_1_out1, demultiplexer_1_out1);
  D_Flip_Flop d_ff_1 (.clk(and_1_out), .D(Pin_on_off_selection), .Q(OPN7));  // open: Qn, preset, en, reset
  and and_3 (and_3_out, Write, Condition_Block, decoder_1_out2, demultiplexer_1_out2);
  D_Flip_Flop d_ff_2 (.clk(and_2_out), .D(Pin_on_off_selection), .Q(OPN6));  // open: Qn, preset, en, reset
  Decoder #(.select(3), .tristate("false")) decoder_1 (
    .out0(decoder_1_out0), .out1(decoder_1_out1), .out2(decoder_1_out2), .out3(decoder_1_out3),
    .out4(decoder_1_out4), .out5(decoder_1_out5), .out6(decoder_1_out6), .out7(decoder_1_out7),
    .sel(Pin_Number));
  and and_4 (and_4_out, Write, Condition_Block, decoder_1_out3, demultiplexer_1_out3);
  D_Flip_Flop d_ff_3 (.clk(and_3_out), .D(Pin_on_off_selection), .Q(OPN5));  // open: Qn, preset, en, reset
  and and_5 (and_5_out, Write, Condition_Block, decoder_1_out4, demultiplexer_1_out4);
  D_Flip_Flop d_ff_4 (.clk(and_4_out), .D(Pin_on_off_selection), .Q(OPN4));  // open: Qn, preset, en, reset
  and and_6 (and_6_out, Write, Condition_Block, decoder_1_out5, demultiplexer_1_out5);
  D_Flip_Flop d_ff_5 (.clk(and_5_out), .D(Pin_on_off_selection), .Q(OPN3));  // open: Qn, preset, en, reset
  Demultiplexer #(.select(3), .width(1), .tristate("false")) demultiplexer_1 (
    .out0(demultiplexer_1_out0), .out1(demultiplexer_1_out1), .out2(demultiplexer_1_out2),
    .out3(demultiplexer_1_out3), .out4(demultiplexer_1_out4), .out5(demultiplexer_1_out5),
    .out6(demultiplexer_1_out6), .out7(demultiplexer_1_out7), .in(not_1_out), .sel(Pin_Number));
  and and_7 (and_7_out, Write, Condition_Block, decoder_1_out6, demultiplexer_1_out6);
  D_Flip_Flop d_ff_6 (.clk(and_6_out), .D(Pin_on_off_selection), .Q(OPN2));  // open: Qn, preset, en, reset
  and and_8 (and_8_out, decoder_1_out7, Write, Condition_Block, demultiplexer_1_out7);
  D_Flip_Flop d_ff_7 (.clk(and_7_out), .D(Pin_on_off_selection), .Q(OPN1));  // open: Qn, preset, en, reset
  not not_1 (not_1_out, CLK);
  D_Flip_Flop d_ff_8 (.clk(and_8_out), .D(Pin_on_off_selection), .Q(OPN0));  // open: Qn, preset, en, reset
endmodule

module Instruction_Decoder_2 (
  input  A31,
  input  A30,
  input  A29,
  input  A28,
  input  A27,
  input  A26,
  input  A25,
  input  A24,
  input  A23,
  input  A22,
  input  A21,
  input  A20,
  input  A19,
  input  A18,
  input  A17,
  input  A16,
  input  A15,
  input  A14,
  input  A13,
  input  A12,
  input  A11,
  input  A10,
  input  A9,
  input  A8,
  input  A7,
  input  A6,
  input  A5,
  input  A4,
  input  A3,
  input  A2,
  input  A1,
  input  A0,
  output reg_rd__rec,
  output reg_wrt__rec,
  output [1:0] reg_adr__rec,
  output iprt_read,
  output iprt_sel,
  output oprt_wrt,
  output oprt_sel,
  output [2:0] bus_out_cntl__rec,
  output reg_rd__snd,
  output [1:0] reg_adr__snd,
  output [2:0] bus_out_cntl__snd
);

  wire and_6_out, and_7_out, and_8_out, and_9_out, and_10_out, and_11_out, and_12_out, and_13_out,
       and_14_out, and_15_out, and_16_out, and_17_out, and_18_out, and_19_out, and_20_out, and_21_out,
       and_22_out, and_23_out, and_24_out, decoder_1_out0, decoder_1_out1, decoder_1_out2, decoder_1_out3,
       decoder_1_out4, decoder_1_out5, decoder_1_out6, decoder_1_out7, decoder_2_out0, decoder_2_out2,
       decoder_2_out3, not_1_out, not_2_out, not_3_out, not_4_out, not_5_out, not_6_out, or_2_out, or_3_out,
       or_4_out, or_5_out, or_6_out, or_7_out, or_8_out, or_9_out, or_10_out;

  and and_1 (reg_rd__rec, decoder_2_out0, or_2_out);
  and and_2 (reg_wrt__rec, decoder_1_out1, decoder_2_out0);
  and and_3 (iprt_read, or_3_out, or_4_out);
  or or_1 (iprt_sel, and_7_out, and_8_out);
  and and_4 (oprt_wrt, decoder_1_out1, decoder_2_out3);
  and and_5 (reg_rd__snd, or_5_out, or_6_out);
  Multiplexer #(.select(1), .width(2)) multiplexer_1 (
    .in0({A22, A23}), .in1({A15, A14}), .out(reg_adr__snd), .sel(not_1_out));
  or or_2 (or_2_out, decoder_1_out0, decoder_1_out3);
  and and_6 (and_6_out, decoder_2_out2, not_2_out);
  or or_3 (or_3_out, and_6_out, and_10_out);
  or or_4 (or_4_out, decoder_1_out0, decoder_1_out1, decoder_1_out3);
  and and_7 (and_7_out, not_3_out, not_5_out, A15, not_6_out);
  and and_8 (and_8_out, decoder_2_out2, not_2_out, A23);
  _8_to_3_priority_encoder u_8_to_3_priority_encoder_1 (
    .A4(and_9_out), .A2(A18), .Q2(bus_out_cntl__rec[2]), .Q1(bus_out_cntl__rec[1]));  // open: A7, A6, A5, A3, A1, A0, Q0
  and and_9 (and_9_out, decoder_1_out0, not_2_out);
  or or_5 (or_5_out, decoder_1_out0, decoder_1_out1);
  or or_6 (or_6_out, and_11_out, and_12_out);
  _8_to_3_priority_encoder u_8_to_3_priority_encoder_2 (
    .A5(or_8_out), .A3(or_7_out), .A2(or_9_out), .A1(and_21_out), .A0(and_22_out), .Q2(bus_out_cntl__snd[2]),
    .Q1(bus_out_cntl__snd[1]), .Q0(bus_out_cntl__snd[0]));  // open: A7, A6, A4
  or or_7 (or_7_out, and_17_out, and_23_out, and_18_out);
  or or_8 (or_8_out, and_14_out, and_16_out);
  or or_9 (or_9_out, and_19_out, and_24_out, and_20_out);
  and and_10 (and_10_out, not_3_out, not_5_out);
  and and_11 (and_11_out, decoder_2_out0, A19, not_2_out);
  and and_12 (and_12_out, not_3_out, A13);
  and and_13 (and_13_out, not_6_out, A18, not_3_out);
  and and_14 (and_14_out, and_13_out, decoder_1_out1);
  and and_15 (and_15_out, not_4_out, A17, A19);
  and and_16 (and_16_out, and_15_out, decoder_1_out1);
  and and_17 (and_17_out, decoder_1_out0, A19, not_2_out);
  and and_18 (and_18_out, decoder_1_out0, not_3_out, not_6_out);
  and and_19 (and_19_out, A19, A18);
  and and_20 (and_20_out, not_3_out, A12);
  and and_21 (and_21_out, decoder_1_out1, decoder_2_out0);
  and and_22 (and_22_out, decoder_1_out1, decoder_2_out3);
  and and_23 (and_23_out, decoder_1_out0, A17, A16);
  and and_24 (and_24_out, A17, not_4_out, or_10_out);
  or or_10 (or_10_out, decoder_1_out0, decoder_1_out1);
  Decoder #(.select(3), .tristate("false")) decoder_1 (
    .out0(decoder_1_out0), .out1(decoder_1_out1), .out2(decoder_1_out2), .out3(decoder_1_out3),
    .out4(decoder_1_out4), .out5(decoder_1_out5), .out6(decoder_1_out6), .out7(decoder_1_out7),
    .sel({A31, A30, A29}));
  not not_1 (not_1_out, A19);
  Decoder #(.select(2), .tristate("false")) decoder_2 (
    .out0(decoder_2_out0), .out2(decoder_2_out2), .out3(decoder_2_out3), .sel({A21, A20}));  // open: out1
  not not_2 (not_2_out, A18);
  not not_3 (not_3_out, A17);
  not not_4 (not_4_out, A16);
  not not_5 (not_5_out, A13);
  not not_6 (not_6_out, A12);

  assign bus_out_cntl__rec[0] = 1'b0;
  assign oprt_sel = A22;
  assign reg_adr__rec = {A23, A22};

  // Notes on the sheet:
  //   Instruction Bits In
endmodule
